// Digital circuit Exam2_1_Template.dig as structural Verilog
module Exam2_1_Template (
  input  reset,
  input  X,
  input  Y,
  input  Z,
  input  load,
  input  clock,
  output A,
  output B,
  output C
);

  wire and_1_out, and_2_out, and_3_out, multiplexer_1_out, multiplexer_2_out, multiplexer_5_out, nA, nB, nC,
       or_1_out, or_2_out, xor_1_out;

  D_FF d_ff_1 (.D(nA), .C(clock), .Q(A));  // open: nQ
  D_FF d_ff_2 (.D(nB), .C(clock), .Q(B));  // open: nQ
  D_FF d_ff_3 (.D(nC), .C(clock), .Q(C));  // open: nQ
  and and_1 (and_1_out, A, B);
  xor xor_1 (xor_1_out, and_1_out, C);
  and and_2 (and_2_out, A, ~B);  // And
  and and_3 (and_3_out, A, C);
  or or_1 (or_1_out, and_2_out, ~C);  // Or
  or or_2 (or_2_out, B, and_3_out);
  Multiplexer multiplexer_1 (.sel(load), .in_0(xor_1_out), .in_1(X), .out(multiplexer_1_out));
  Multiplexer multiplexer_2 (.sel(load), .in_0(or_1_out), .in_1(Y), .out(multiplexer_2_out));
  Multiplexer multiplexer_3 (.sel(reset), .in_0(multiplexer_1_out), .in_1(1'b0), .out(nA));
  Multiplexer multiplexer_4 (.sel(reset), .in_0(multiplexer_2_out), .in_1(1'b0), .out(nB));
  Multiplexer multiplexer_5 (.sel(load), .in_0(or_2_out), .in_1(Z), .out(multiplexer_5_out));
  Multiplexer multiplexer_6 (.sel(reset), .in_0(multiplexer_5_out), .in_1(1'b0), .out(nC));
endmodule

/* Test case T06:
X Y Z reset load clock A B C
0 0 0 1 0 0 x x x
0 0 0 1 0 1 0 0 0
1 1 0 0 1 0 0 0 0
1 1 0 0 1 1 1 1 0
0 0 0 0 0 0 1 1 0
0 0 0 0 0 1 1 1 1
0 0 0 0 0 0 1 1 1
0 0 0 0 0 1 0 0 1
0 0 0 0 0 0 0 0 1
0 0 0 0 0 1 1 0 0
0 0 0 0 0 0 1 0 0
0 0 0 0 0 1 0 1 0
0 0 0 0 0 0 0 1 0
0 0 0 0 0 1 0 1 1
0 0 0 0 0 0 0 1 1
0 0 0 0 0 1 1 0 1
0 0 0 0 0 0 1 0 1
0 0 0 0 0 1 1 1 1
0 0 0 0 0 0 1 1 1
0 0 0 0 0 1 0 0 1
0 0 0 0 0 0 0 0 1
*/
