// Digital circuit Exam2_2_Template.dig as structural Verilog
module Exam2_2_Template (
  input  reset,
  input  [15:0] P,
  input  start,
  input  clock,
  output [15:0] W,
  output [15:0] H,
  output [31:0] A,
  output busy
);

  wire d_ff_1_nq, d_ff_1_q, multiplexer_1_out, s;
  wire [15:0] add_1_s, d_ff_2_q, d_ff_3_q, div_1_q, div_2_q, div_2_r, multiplexer_2_out, multiplexer_3_out,
       multiplexer_5_out, multiplexer_6_out;
  wire [31:0] d_ff_4_q, mul_1_mul, multiplexer_4_out, multiplexer_7_out;

  Div #(.Bits(16)) div_1 (.a(P), .b(16'h2), .q(div_1_q));  // open: r
  D_FF d_ff_1 (.D(start), .C(clock), .Q(d_ff_1_q), .nQ(d_ff_1_nq));
  // Probe on d_ff_1_q
  Div #(.Bits(16)) div_2 (.a(div_1_q), .b(16'h2), .q(div_2_q), .r(div_2_r));
  and and_1 (s, start, d_ff_1_nq);
  Add #(.Bits(16)) add_1 (.a(div_2_q), .b(div_2_r), .c_i(1'b0), .s(add_1_s));  // open: c_o
  Mul #(.Bits(16)) mul_1 (.a(div_2_q), .b(add_1_s), .mul(mul_1_mul));
  D_FF #(.Bits(16)) d_ff_2 (.D(div_2_q), .C(clock), .Q(d_ff_2_q));  // open: nQ
  D_FF #(.Bits(16)) d_ff_3 (.D(add_1_s), .C(clock), .Q(d_ff_3_q));  // open: nQ
  D_FF #(.Bits(32)) d_ff_4 (.D(mul_1_mul), .C(clock), .Q(d_ff_4_q));  // open: nQ
  Multiplexer multiplexer_1 (.sel(reset), .in_0(s), .in_1(1'b0), .out(multiplexer_1_out));
  Multiplexer #(.Bits(16)) multiplexer_2 (.sel(busy), .in_0(H), .in_1(d_ff_2_q), .out(multiplexer_2_out));
  Multiplexer #(.Bits(16)) multiplexer_3 (.sel(busy), .in_0(W), .in_1(d_ff_3_q), .out(multiplexer_3_out));
  Multiplexer #(.Bits(32)) multiplexer_4 (.sel(busy), .in_0(A), .in_1(d_ff_4_q), .out(multiplexer_4_out));
  D_FF d_ff_5 (.D(multiplexer_1_out), .C(clock), .Q(busy));  // open: nQ
  Multiplexer #(.Bits(16)) multiplexer_5 (
    .sel(reset), .in_0(multiplexer_2_out), .in_1({16{1'b0}}), .out(multiplexer_5_out));
  Multiplexer #(.Bits(16)) multiplexer_6 (
    .sel(reset), .in_0(multiplexer_3_out), .in_1({16{1'b0}}), .out(multiplexer_6_out));
  Multiplexer #(.Bits(32)) multiplexer_7 (
    .sel(reset), .in_0(multiplexer_4_out), .in_1({32{1'b0}}), .out(multiplexer_7_out));
  D_FF #(.Bits(16)) d_ff_6 (.D(multiplexer_5_out), .C(clock), .Q(H));  // open: nQ
  D_FF #(.Bits(16)) d_ff_7 (.D(multiplexer_6_out), .C(clock), .Q(W));  // open: nQ
  D_FF #(.Bits(32)) d_ff_8 (.D(multiplexer_7_out), .C(clock), .Q(A));  // open: nQ

  // Other names for the same wires on the sheet: clk = clock; r = reset
endmodule

/* Test case T01:
P start clock reset W H A busy
0 0 0 1 x x x x
0 0 1 1 x x x x
0 0 0 0 0 0 0 0
0 0 1 0 0 0 0 0
92 1 0 0 x x x x
92 1 1 0 x x x x
0 0 0 0 x x x x
0 0 1 0 x x x x
0 0 0 0 x x x x
0 0 1 0 x x x x
0 0 0 0 x x x x
0 0 1 0 x x x x
0 0 0 0 x x x x
0 0 1 0 x x x x
0 0 0 0 x x x x
0 0 1 0 x x x x
0 0 0 0 x x x x
0 0 1 0 x x x x
0 0 0 0 x x x x
0 0 1 0 x x x x
0 0 0 0 x x x x
0 0 1 0 x x x x
0 0 0 0 x x x x
0 0 1 0 x x x x
0 0 0 0 x x x x
0 0 1 0 x x x x
0 0 0 0 x x x x
0 0 1 0 x x x x
0 0 0 0 x x x x
0 0 1 0 x x x x
0 0 0 0 x x x x
0 0 1 0 x x x x
0 0 0 0 x x x x
0 0 1 0 x x x x
0 0 0 0 x x x x
0 0 1 0 x x x x
0 0 0 0 x x x x
0 0 1 0 x x x x
0 0 0 0 x x x x
0 0 1 0 x x x x
0 0 0 0 x x x x
0 0 1 0 x x x x
0 0 0 0 x x x x
0 0 1 0 x x x x
0 0 0 0 x x x x
0 0 1 0 x x x x
0 0 0 0 x x x x
0 0 1 0 x x x x
0 0 0 0 x x x x
0 0 1 0 x x x x
0 0 0 0 x x x x
0 0 1 0 x x x x
0 0 0 0 x x x x
0 0 1 0 x x x x
0 0 0 0 x x x x
0 0 1 0 x x x x
0 0 0 0 x x x x
0 0 1 0 x x x x
0 0 0 0 x x x x
0 0 1 0 x x x x
0 0 0 0 x x x x
0 0 1 0 x x x x
0 0 0 0 x x x x
0 0 1 0 x x x x
0 0 0 0 x x x x
0 0 1 0 x x x x
0 0 0 0 x x x x
0 0 1 0 x x x x
0 0 0 0 x x x x
0 0 1 0 x x x x
0 0 0 0 x x x x
0 0 1 0 x x x x
0 0 0 0 x x x x
0 0 1 0 x x x x
0 0 0 0 x x x x
0 0 1 0 x x x x
0 0 0 0 x x x x
0 0 1 0 x x x x
0 0 0 0 x x x x
0 0 1 0 x x x x
0 0 0 0 x x x x
0 0 1 0 x x x x
0 0 0 0 x x x x
0 0 1 0 x x x x
0 0 0 0 x x x x
0 0 1 0 x x x x
0 0 0 0 x x x x
0 0 1 0 x x x x
0 0 0 0 x x x x
0 0 1 0 x x x x
0 0 0 0 x x x x
0 0 1 0 x x x x
0 0 0 0 x x x x
0 0 1 0 x x x x
0 0 0 0 x x x x
0 0 1 0 x x x x
0 0 0 0 x x x x
0 0 1 0 x x x x
0 0 0 0 x x x x
0 0 1 0 x x x x
0 0 0 0 x x x x
0 0 1 0 x x x x
0 0 0 0 x x x x
0 0 1 0 x x x x
0 0 0 0 x x x x
0 0 1 0 x x x x
0 0 0 0 x x x x
0 0 1 0 x x x x
0 0 0 0 x x x x
0 0 1 0 x x x x
0 0 0 0 x x x x
0 0 1 0 x x x x
0 0 0 0 x x x x
0 0 1 0 x x x x
0 0 0 0 x x x x
0 0 1 0 x x x x
0 0 0 0 x x x x
0 0 1 0 x x x x
0 0 0 0 x x x x
0 0 1 0 x x x x
0 0 0 0 x x x x
0 0 1 0 x x x x
0 0 0 0 x x x x
0 0 1 0 x x x x
0 0 0 0 x x x x
0 0 1 0 x x x x
0 0 0 0 x x x x
0 0 1 0 x x x x
0 0 0 0 x x x x
0 0 1 0 x x x x
0 0 0 0 x x x x
0 0 1 0 x x x x
0 0 0 0 x x x x
0 0 1 0 x x x x
0 0 0 0 x x x x
0 0 1 0 x x x x
0 0 0 0 x x x x
0 0 1 0 x x x x
0 0 0 0 x x x x
0 0 1 0 x x x x
0 0 0 0 x x x x
0 0 1 0 x x x x
0 0 0 0 x x x x
0 0 1 0 x x x x
0 0 0 0 x x x x
0 0 1 0 x x x x
0 0 0 0 x x x x
0 0 1 0 x x x x
0 0 0 0 x x x x
0 0 1 0 x x x x
0 0 0 0 x x x x
0 0 1 0 x x x x
0 0 0 0 x x x x
0 0 1 0 x x x x
0 0 0 0 x x x x
0 0 1 0 x x x x
0 0 0 0 x x x x
0 0 1 0 x x x x
0 0 0 0 x x x x
0 0 1 0 x x x x
0 0 0 0 x x x x
0 0 1 0 x x x x
0 0 0 0 x x x x
0 0 1 0 x x x x
0 0 0 0 x x x x
0 0 1 0 x x x x
0 0 0 0 x x x x
0 0 1 0 x x x x
0 0 0 0 x x x x
0 0 1 0 x x x x
0 0 0 0 x x x x
0 0 1 0 x x x x
0 0 0 0 x x x x
0 0 1 0 x x x x
0 0 0 0 x x x x
0 0 1 0 x x x x
0 0 0 0 x x x x
0 0 1 0 x x x x
0 0 0 0 x x x x
0 0 1 0 x x x x
0 0 0 0 x x x x
0 0 1 0 x x x x
0 0 0 0 x x x x
0 0 1 0 x x x x
0 0 0 0 x x x x
0 0 1 0 x x x x
0 0 0 0 x x x x
0 0 1 0 x x x x
0 0 0 0 x x x x
0 0 1 0 x x x x
0 0 0 0 x x x x
0 0 1 0 x x x x
0 0 0 0 x x x x
0 0 1 0 x x x x
0 0 0 0 x x x x
0 0 1 0 x x x x
0 0 0 0 x x x x
0 0 1 0 x x x x
0 0 0 0 x x x x
0 0 1 0 x x x x
0 0 0 0 x x x x
0 0 1 0 x x x x
0 0 0 0 x x x x
0 0 1 0 x x x x
0 0 0 0 x x x x
0 0 1 0 x x x x
0 0 0 0 x x x x
0 0 1 0 x x x x
0 0 0 0 x x x x
0 0 1 0 x x x x
0 0 0 0 x x x x
0 0 1 0 x x x x
0 0 0 0 x x x x
0 0 1 0 x x x x
0 0 0 0 x x x x
0 0 1 0 x x x x
0 0 0 0 x x x x
0 0 1 0 x x x x
0 0 0 0 x x x x
0 0 1 0 x x x x
0 0 0 0 x x x x
0 0 1 0 x x x x
0 0 0 0 x x x x
0 0 1 0 x x x x
0 0 0 0 x x x x
0 0 1 0 x x x x
0 0 0 0 x x x x
0 0 1 0 x x x x
0 0 0 0 x x x x
0 0 1 0 x x x x
0 0 0 0 x x x x
0 0 1 0 x x x x
0 0 0 0 x x x x
0 0 1 0 x x x x
0 0 0 0 x x x x
0 0 1 0 x x x x
0 0 0 0 x x x x
0 0 1 0 x x x x
0 0 0 0 x x x x
0 0 1 0 x x x x
0 0 0 0 x x x x
0 0 1 0 x x x x
0 0 0 0 x x x x
0 0 1 0 x x x x
0 0 0 0 x x x x
0 0 1 0 x x x x
0 0 0 0 x x x x
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*/
