// Digital circuit Exam_2_3.dig as structural Verilog
module Exam_2_3 (
  input  reset,
  input  [7:0] N,
  input  \new ,
  input  clock,
  output [7:0] num_inc,
  output [7:0] max,
  output busy
);

  wire comparator_3_gt, DoneC, multiplexer_1_out, multiplexer_3_out, multiplexer_5_out, startC;
  wire [1:0] multiplexer_2_out, multiplexer_4_out, multiplexer_7_out, multiplexer_10_out, state;
  wire [7:0] add_1_s, multiplexer_6_out, multiplexer_8_out, multiplexer_9_out, multiplexer_11_out,
       multiplexer_12_out, n_t;

  D_FF #(.Bits(8)) d_ff_1 (.D(N), .C(clock), .Q(n_t));  // open: nQ
  Comparator #(.Bits(2)) comparator_1 (.a(state), .b(2'b01), .eq(startC));  // open: gt, lt
  Comparator #(.Bits(2)) comparator_2 (.a(state), .b(2'b10), .eq(DoneC));  // open: gt, lt
  Multiplexer multiplexer_1 (.sel(startC), .in_0(busy), .in_1(1'b1), .out(multiplexer_1_out));
  Comparator #(.Bits(8)) comparator_3 (.a(n_t), .b(max), .gt(comparator_3_gt));  // open: eq, lt
  Multiplexer #(.Bits(2)) multiplexer_2 (.sel(\new ), .in_0(state), .in_1(2'b01), .out(multiplexer_2_out));
  Multiplexer multiplexer_3 (.sel(DoneC), .in_0(multiplexer_1_out), .in_1(1'b0), .out(multiplexer_3_out));
  Add #(.Bits(8)) add_1 (.a(num_inc), .b({8{1'b0}}), .c_i(comparator_3_gt), .s(add_1_s));  // open: c_o
  Multiplexer #(.Bits(2)) multiplexer_4 (.sel(startC), .in_0(multiplexer_2_out), .in_1(2'b10), .out(multiplexer_4_out));
  Multiplexer multiplexer_5 (.sel(reset), .in_0(multiplexer_3_out), .in_1(1'b0), .out(multiplexer_5_out));
  Multiplexer #(.Bits(8)) multiplexer_6 (.sel(comparator_3_gt), .in_0(max), .in_1(n_t), .out(multiplexer_6_out));
  Multiplexer #(.Bits(2)) multiplexer_7 (.sel(DoneC), .in_0(multiplexer_4_out), .in_1(2'b00), .out(multiplexer_7_out));
  D_FF d_ff_2 (.D(multiplexer_5_out), .C(clock), .Q(busy));  // open: nQ
  Multiplexer #(.Bits(8)) multiplexer_8 (.sel(startC), .in_0(num_inc), .in_1(add_1_s), .out(multiplexer_8_out));
  Multiplexer #(.Bits(8)) multiplexer_9 (.sel(startC), .in_0(max), .in_1(multiplexer_6_out), .out(multiplexer_9_out));
  Multiplexer #(.Bits(2)) multiplexer_10 (
    .sel(reset), .in_0(multiplexer_7_out), .in_1(2'b00), .out(multiplexer_10_out));
  D_FF #(.Bits(2)) d_ff_3 (.D(multiplexer_10_out), .C(clock), .Q(state));  // open: nQ
  Multiplexer #(.Bits(8)) multiplexer_11 (
    .sel(reset), .in_0(multiplexer_8_out), .in_1({8{1'b0}}), .out(multiplexer_11_out));
  Multiplexer #(.Bits(8)) multiplexer_12 (
    .sel(reset), .in_0(multiplexer_9_out), .in_1({8{1'b0}}), .out(multiplexer_12_out));
  D_FF #(.Bits(8)) d_ff_4 (.D(multiplexer_11_out), .C(clock), .Q(num_inc));  // open: nQ
  D_FF #(.Bits(8)) d_ff_5 (.D(multiplexer_12_out), .C(clock), .Q(max));  // open: nQ

  // Other names for the same wires on the sheet: clk = clock; r = reset

  // Notes on the sheet:
  //   New pass D-FF
  //   to Set State -> N also D-FF
  //   state
  //   00 : idel
  //   01 : startC get the N
  //   02 : doneC already process N
  //   00 : after 02 back to 00
  //   busy
  //   01 : startC busy=1
  //   02 : doneC busy=0
endmodule

/* Test case T06:
N new reset clock num_inc max busy
0 0 1 0 x x x
0 0 1 1 0 0 0
131 1 0 0 x x x
131 1 0 1 x x x
0 0 0 0 x x x
0 0 0 1 x x x
0 0 0 0 x x x
0 0 0 1 x x x
0 0 0 0 x x x
0 0 0 1 x x x
0 0 0 0 x x x
0 0 0 1 x x x
0 0 0 0 x x x
0 0 0 1 x x x
0 0 0 0 x x x
0 0 0 1 x x x
0 0 0 0 x x x
0 0 0 1 x x x
0 0 0 0 x x x
0 0 0 1 x x x
0 0 0 0 x x x
0 0 0 1 x x x
0 0 0 0 x x x
0 0 0 1 x x x
0 0 0 0 x x x
0 0 0 1 x x x
0 0 0 0 x x x
0 0 0 1 x x x
0 0 0 0 x x x
0 0 0 1 x x x
0 0 0 0 x x x
0 0 0 1 x x x
0 0 0 0 x x x
0 0 0 1 x x x
0 0 0 0 x x x
0 0 0 1 x x x
0 0 0 0 x x x
0 0 0 1 x x x
0 0 0 0 x x x
0 0 0 1 x x x
0 0 0 0 x x x
0 0 0 1 x x x
0 0 0 0 x x x
0 0 0 1 x x x
0 0 0 0 x x x
0 0 0 1 x x x
0 0 0 0 x x x
0 0 0 1 x x x
0 0 0 0 x x x
0 0 0 1 x x x
0 0 0 0 x x x
0 0 0 1 x x x
0 0 0 0 x x x
0 0 0 1 x x x
0 0 0 0 x x x
0 0 0 1 x x x
0 0 0 0 x x x
0 0 0 1 x x x
0 0 0 0 x x x
0 0 0 1 x x x
0 0 0 0 x x x
0 0 0 1 x x x
0 0 0 0 x x x
0 0 0 1 x x x
0 0 0 0 1 131 0
0 0 0 1 1 131 0
130 1 0 0 x x x
130 1 0 1 x x x
0 0 0 0 x x x
0 0 0 1 x x x
0 0 0 0 x x x
0 0 0 1 x x x
0 0 0 0 x x x
0 0 0 1 x x x
0 0 0 0 x x x
0 0 0 1 x x x
0 0 0 0 x x x
0 0 0 1 x x x
0 0 0 0 x x x
0 0 0 1 x x x
0 0 0 0 x x x
0 0 0 1 x x x
0 0 0 0 x x x
0 0 0 1 x x x
0 0 0 0 x x x
0 0 0 1 x x x
0 0 0 0 x x x
0 0 0 1 x x x
0 0 0 0 x x x
0 0 0 1 x x x
0 0 0 0 x x x
0 0 0 1 x x x
0 0 0 0 x x x
0 0 0 1 x x x
0 0 0 0 x x x
0 0 0 1 x x x
0 0 0 0 x x x
0 0 0 1 x x x
0 0 0 0 x x x
0 0 0 1 x x x
0 0 0 0 x x x
0 0 0 1 x x x
0 0 0 0 x x x
0 0 0 1 x x x
0 0 0 0 x x x
0 0 0 1 x x x
0 0 0 0 x x x
0 0 0 1 x x x
0 0 0 0 x x x
0 0 0 1 x x x
0 0 0 0 x x x
0 0 0 1 x x x
0 0 0 0 x x x
0 0 0 1 x x x
0 0 0 0 x x x
0 0 0 1 x x x
0 0 0 0 x x x
0 0 0 1 x x x
0 0 0 0 x x x
0 0 0 1 x x x
0 0 0 0 x x x
0 0 0 1 x x x
0 0 0 0 x x x
0 0 0 1 x x x
0 0 0 0 x x x
0 0 0 1 x x x
0 0 0 0 x x x
0 0 0 1 x x x
0 0 0 0 1 131 0
0 0 0 1 1 131 0
58 1 0 0 x x x
58 1 0 1 x x x
0 0 0 0 x x x
0 0 0 1 x x x
0 0 0 0 x x x
0 0 0 1 x x x
0 0 0 0 x x x
0 0 0 1 x x x
0 0 0 0 x x x
0 0 0 1 x x x
0 0 0 0 x x x
0 0 0 1 x x x
0 0 0 0 x x x
0 0 0 1 x x x
0 0 0 0 x x x
0 0 0 1 x x x
0 0 0 0 x x x
0 0 0 1 x x x
0 0 0 0 x x x
0 0 0 1 x x x
0 0 0 0 x x x
0 0 0 1 x x x
0 0 0 0 x x x
0 0 0 1 x x x
0 0 0 0 x x x
0 0 0 1 x x x
0 0 0 0 x x x
0 0 0 1 x x x
0 0 0 0 x x x
0 0 0 1 x x x
0 0 0 0 x x x
0 0 0 1 x x x
0 0 0 0 x x x
0 0 0 1 x x x
0 0 0 0 x x x
0 0 0 1 x x x
0 0 0 0 x x x
0 0 0 1 x x x
0 0 0 0 x x x
0 0 0 1 x x x
0 0 0 0 x x x
0 0 0 1 x x x
0 0 0 0 x x x
0 0 0 1 x x x
0 0 0 0 x x x
0 0 0 1 x x x
0 0 0 0 x x x
0 0 0 1 x x x
0 0 0 0 x x x
0 0 0 1 x x x
0 0 0 0 x x x
0 0 0 1 x x x
0 0 0 0 x x x
0 0 0 1 x x x
0 0 0 0 x x x
0 0 0 1 x x x
0 0 0 0 x x x
0 0 0 1 x x x
0 0 0 0 x x x
0 0 0 1 x x x
0 0 0 0 x x x
0 0 0 1 x x x
0 0 0 0 1 131 0
0 0 0 1 1 131 0
154 1 0 0 x x x
154 1 0 1 x x x
0 0 0 0 x x x
0 0 0 1 x x x
0 0 0 0 x x x
0 0 0 1 x x x
0 0 0 0 x x x
0 0 0 1 x x x
0 0 0 0 x x x
0 0 0 1 x x x
0 0 0 0 x x x
0 0 0 1 x x x
0 0 0 0 x x x
0 0 0 1 x x x
0 0 0 0 x x x
0 0 0 1 x x x
0 0 0 0 x x x
0 0 0 1 x x x
0 0 0 0 x x x
0 0 0 1 x x x
0 0 0 0 x x x
0 0 0 1 x x x
0 0 0 0 x x x
0 0 0 1 x x x
0 0 0 0 x x x
0 0 0 1 x x x
0 0 0 0 x x x
0 0 0 1 x x x
0 0 0 0 x x x
0 0 0 1 x x x
0 0 0 0 x x x
0 0 0 1 x x x
0 0 0 0 x x x
0 0 0 1 x x x
0 0 0 0 x x x
0 0 0 1 x x x
0 0 0 0 x x x
0 0 0 1 x x x
0 0 0 0 x x x
0 0 0 1 x x x
0 0 0 0 x x x
0 0 0 1 x x x
0 0 0 0 x x x
0 0 0 1 x x x
0 0 0 0 x x x
0 0 0 1 x x x
0 0 0 0 x x x
0 0 0 1 x x x
0 0 0 0 x x x
0 0 0 1 x x x
0 0 0 0 x x x
0 0 0 1 x x x
0 0 0 0 x x x
0 0 0 1 x x x
0 0 0 0 x x x
0 0 0 1 x x x
0 0 0 0 x x x
0 0 0 1 x x x
0 0 0 0 x x x
0 0 0 1 x x x
0 0 0 0 x x x
0 0 0 1 x x x
0 0 0 0 2 154 0
0 0 0 1 2 154 0
122 1 0 0 x x x
122 1 0 1 x x x
0 0 0 0 x x x
0 0 0 1 x x x
0 0 0 0 x x x
0 0 0 1 x x x
0 0 0 0 x x x
0 0 0 1 x x x
0 0 0 0 x x x
0 0 0 1 x x x
0 0 0 0 x x x
0 0 0 1 x x x
0 0 0 0 x x x
0 0 0 1 x x x
0 0 0 0 x x x
0 0 0 1 x x x
0 0 0 0 x x x
0 0 0 1 x x x
0 0 0 0 x x x
0 0 0 1 x x x
0 0 0 0 x x x
0 0 0 1 x x x
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*/
