// Digital circuit Final2023_1.dig as structural Verilog
module Final2023_1 (
  input  [7:0] A,
  input  reset,
  input  clk,
  output [11:0] \output 
);

  wire Add_out, and_1_out, d_ff_1_nq;
  wire [11:0] add_2_s, multiplexer_1_out, multiplexer_2_out;

  Seven_Seg_Hex seven_seg_hex_1 (.d(A[7:4]), .dp(1'b1));
  Seven_Seg_Hex seven_seg_hex_2 (.d(A[3:0]), .dp(1'b1));
  Button Add (.out(Add_out));
  D_FF d_ff_1 (.D(Add_out), .C(clk), .nQ(d_ff_1_nq));  // open: Q
  Add #(.Bits(12)) add_2 (.a(\output ), .b({4'b0000, A}), .c_i(1'b0), .s(add_2_s));  // open: c_o
  and and_1 (and_1_out, Add_out, d_ff_1_nq);
  Multiplexer #(.Bits(12)) multiplexer_1 (.sel(and_1_out), .in_0(\output ), .in_1(add_2_s), .out(multiplexer_1_out));
  Multiplexer #(.Bits(12)) multiplexer_2 (
    .sel(reset), .in_0(multiplexer_1_out), .in_1({12{1'b0}}), .out(multiplexer_2_out));
  Seven_Seg_Hex seven_seg_hex_3 (.d(\output [11:8]), .dp(1'b1));
  D_FF #(.Bits(12)) d_ff_2 (.D(multiplexer_2_out), .C(clk), .Q(\output ));  // open: nQ
  Seven_Seg_Hex seven_seg_hex_4 (.d(\output [7:4]), .dp(1'b1));
  Seven_Seg_Hex seven_seg_hex_5 (.d(\output [3:0]), .dp(1'b1));
endmodule
