// Digital circuit 2023_2.dig as structural Verilog
module _2023_2 (
  input  clk,
  input  Push,
  output [3:0] V
);

  wire and_1_out, and_2_out, and_3_out, and_4_out, and_5_out, comparator_1_eq, d_ff_2_nq, d_ff_3_nq,
       multiplexer_3_out, multiplexer_4_out, not_1_out, not_2_out, not_3_out, or_1_out, Ostate, Sstate, state;
  wire [3:0] add_1_s, multiplexer_2_out, multiplexer_5_out;

  D_FF d_ff_1 (.D(state), .C(clk), .Q(Ostate));  // open: nQ
  Multiplexer multiplexer_1 (.sel(and_1_out), .in_0(Sstate), .in_1(1'b1), .out(Sstate));
  D_FF d_ff_2 (.D(Push), .C(clk), .nQ(d_ff_2_nq));  // open: Q
  and and_1 (and_1_out, Push, d_ff_2_nq);
  D_FF d_ff_3 (.D(Push), .C(clk), .nQ(d_ff_3_nq));  // open: Q
  Add #(.Bits(4)) add_1 (.a(V), .b(4'b0011), .c_i(1'b0), .s(add_1_s));  // open: c_o
  and and_2 (and_2_out, not_1_out, Ostate);
  not not_1 (not_1_out, state);
  and and_3 (and_3_out, Push, d_ff_3_nq);
  and and_4 (and_4_out, and_1_out, not_2_out);
  not not_2 (not_2_out, state);
  Multiplexer #(.Bits(4)) multiplexer_2 (.sel(and_4_out), .in_0(V), .in_1(add_1_s), .out(multiplexer_2_out));
  or or_1 (or_1_out, not_3_out, and_2_out);
  not not_3 (not_3_out, Sstate);
  Comparator #(.Bits(4)) comparator_1 (.a(V), .b(4'b1111), .eq(comparator_1_eq));  // open: gt, lt
  and and_5 (and_5_out, and_3_out, state);
  Multiplexer multiplexer_3 (.sel(comparator_1_eq), .in_0(state), .in_1(1'b1), .out(multiplexer_3_out));
  Multiplexer multiplexer_4 (.sel(and_5_out), .in_0(multiplexer_3_out), .in_1(1'b0), .out(multiplexer_4_out));
  Multiplexer #(.Bits(4)) multiplexer_5 (
    .sel(or_1_out), .in_0(multiplexer_2_out), .in_1(4'b0011), .out(multiplexer_5_out));
  Seven_Seg_Hex seven_seg_hex_1 (.d(V), .dp(1'b1));
  D_FF #(.Bits(4)) d_ff_4 (.D(multiplexer_5_out), .C(clk), .Q(V));  // open: nQ
  D_FF d_ff_5 (.D(multiplexer_4_out), .C(clk), .Q(state));  // open: nQ
  // Probe on state
endmodule
