// Digital circuit 2023_3.dig as structural Verilog
module _2023_3 (
  input  [15:0] A,
  input  reset,
  input  \input ,
  input  clk,
  output [15:0] second,
  output [15:0] out_6
);

  wire and_1_out, and_2_out, and_3_out, comparator_1_eq, comparator_1_gt, comparator_2_eq, comparator_2_gt,
       comparator_3_eq, comparator_3_gt, or_1_out, or_2_out, or_3_out;
  wire [15:0] multiplexer_1_out, multiplexer_2_out, multiplexer_3_out, multiplexer_4_out, multiplexer_5_out;

  Comparator #(.Bits(16)) comparator_1 (.a(A), .b(second), .gt(comparator_1_gt), .eq(comparator_1_eq));  // open: lt
  or or_1 (or_1_out, comparator_1_gt, comparator_1_eq);
  Comparator #(.Bits(16)) comparator_2 (.a(A), .b(out_6), .gt(comparator_2_gt), .eq(comparator_2_eq));  // open: lt
  or or_2 (or_2_out, comparator_2_gt, comparator_2_eq);
  and and_1 (and_1_out, or_1_out, \input );
  Multiplexer #(.Bits(16)) multiplexer_1 (.sel(and_1_out), .in_0(second), .in_1(A), .out(multiplexer_1_out));
  Comparator #(.Bits(16)) comparator_3 (.a(A), .b(out_6), .gt(comparator_3_gt), .eq(comparator_3_eq));  // open: lt
  and and_2 (and_2_out, or_2_out, \input );
  or or_3 (or_3_out, comparator_3_gt, comparator_3_eq);
  Multiplexer #(.Bits(16)) multiplexer_2 (.sel(and_2_out), .in_0(out_6), .in_1(A), .out(multiplexer_2_out));
  and and_3 (and_3_out, or_3_out, \input );
  Multiplexer #(.Bits(16)) multiplexer_3 (
    .sel(reset), .in_0(multiplexer_2_out), .in_1({16{1'b0}}), .out(multiplexer_3_out));
  Multiplexer #(.Bits(16)) multiplexer_4 (
    .sel(and_3_out), .in_0(multiplexer_1_out), .in_1(out_6), .out(multiplexer_4_out));
  D_FF #(.Bits(16)) d_ff_1 (.D(multiplexer_3_out), .C(clk), .Q(out_6));  // open: nQ
  Multiplexer #(.Bits(16)) multiplexer_5 (
    .sel(reset), .in_0(multiplexer_4_out), .in_1({16{1'b0}}), .out(multiplexer_5_out));
  D_FF #(.Bits(16)) d_ff_2 (.D(multiplexer_5_out), .C(clk), .Q(second));  // open: nQ

  // Other names for the same wires on the sheet: max[15:0] = out_6; Smax[15:0] = second
endmodule

/* Test case Case1:
clk A input reset second
0 0 0 0 0
1 0 0 0 0
0 0 0 1 0
1 0 0 1 0
0 0  0 0 0
1 0  0 0 0
0 5 1 0 X
1 5 1 0 X
0  0 0 0 0
1  0 0 0 0
0 12 1 0 X
1 12 1 0 X
0  0 0 0 X
1  0 0 0 5
*/

/* Test case Case2:
clk A input reset second
0 0 0 0 0
1 0 0 0 0
0 0 0 1 0
1 0 0 1 0
0 0  0 0 0
1 0  0 0 0
0 5 1 0 X
1 5 1 0 X
0  0 0 0 0
1  0 0 0 0
0 15 1 0 X
1 15 1 0 X
0  0 0 0 X
1  0 0 0 5
*/

/* Test case Case3:
clk A input reset second
0 0 0 0 0
1 0 0 0 0
0 0 0 1 0
1 0 0 1 0
0 0  0 0 0
1 0  0 0 0
0 65535 1 0 X
1 65535 1 0 X
0  0 0 0 0
1  0 0 0 0
0 65524 1 0 X
1 65524 1 0 X
0  0 0 0 X
1  0 0 0 65524
*/
