// Digital circuit 2023_final_2.dig as structural Verilog
module _2023_final_2 (
  input  [15:0] A,
  input  \input ,
  input  clk,
  output [7:0] sqrt,
  output busy,
  output [7:0] L,
  output [7:0] R
);

  wire and_1_out, and_2_out, comparator_1_gt, found, isEqual, isLess, isMore, multiplexer_4_out,
       multiplexer_5_out, or_1_out;
  wire [7:0] add_1_s, add_2_s, mid, multiplexer_6_out, multiplexer_7_out, multiplexer_8_out,
       multiplexer_9_out, sub_1_s;
  wire [15:0] A_t, mul_1_mul;

  Add #(.Bits(8)) add_1 (.a(L), .b(R), .c_i(1'b0), .s(add_1_s));  // open: c_o
  Mul #(.Bits(8)) mul_1 (.a(mid), .b(mid), .mul(mul_1_mul));
  Comparator #(.Bits(8)) comparator_1 (.a(L), .b(R), .gt(comparator_1_gt));  // open: eq, lt
  Div #(.Bits(8)) div_1 (.a(add_1_s), .b(8'h2), .q(mid));  // open: r
  // Probe on mul_1_mul
  or or_1 (or_1_out, isEqual, comparator_1_gt);
  Comparator #(.Bits(16)) comparator_2 (.a(mul_1_mul), .b(A_t), .gt(isMore), .eq(isEqual), .lt(isLess));
  Multiplexer #(.Bits(16)) multiplexer_1 (.sel(\input ), .in_0(A_t), .in_1(A), .out(A_t));
  // Probe on A_t
  Multiplexer #(.Bits(8)) multiplexer_2 (.sel(busy), .in_0(sqrt), .in_1(mid), .out(sqrt));
  Multiplexer multiplexer_3 (.sel(\input ), .in_0(or_1_out), .in_1(1'b0), .out(found));
  Sub #(.Bits(8)) sub_1 (.a(mid), .b(8'h1), .c_i(1'b0), .s(sub_1_s));  // open: c_o
  Multiplexer multiplexer_4 (.sel(\input ), .in_0(busy), .in_1(1'b1), .out(multiplexer_4_out));
  Add #(.Bits(8)) add_2 (.a(mid), .b(8'h1), .c_i(1'b0), .s(add_2_s));  // open: c_o
  Multiplexer multiplexer_5 (.sel(found), .in_0(multiplexer_4_out), .in_1(1'b0), .out(multiplexer_5_out));
  and and_1 (and_1_out, isLess, busy);
  and and_2 (and_2_out, isMore, busy);
  D_FF d_ff_1 (.D(multiplexer_5_out), .C(clk), .Q(busy));  // open: nQ
  Multiplexer #(.Bits(8)) multiplexer_6 (.sel(and_1_out), .in_0(L), .in_1(add_2_s), .out(multiplexer_6_out));
  Multiplexer #(.Bits(8)) multiplexer_7 (.sel(and_2_out), .in_0(R), .in_1(sub_1_s), .out(multiplexer_7_out));
  Multiplexer #(.Bits(8)) multiplexer_8 (.sel(\input ), .in_0(multiplexer_6_out), .in_1(8'h1), .out(multiplexer_8_out));
  Multiplexer #(.Bits(8)) multiplexer_9 (
    .sel(\input ), .in_0(multiplexer_7_out), .in_1(A_t[7:0]), .out(multiplexer_9_out));
  D_FF #(.Bits(8)) d_ff_2 (.D(multiplexer_8_out), .C(clk), .Q(L));  // open: nQ
  D_FF #(.Bits(8)) d_ff_3 (.D(multiplexer_9_out), .C(clk), .Q(R));  // open: nQ

  // Other names for the same wires on the sheet: ans[7:0] = sqrt
endmodule

/* Test case TestCase1:
clk A input sqrt busy
0 0 0 0 0
1 0 0 0 0
0 0 0 0 0
1 0 0 0 0
0 0 1 X X
1 0 1 X X
repeat (80) C 0 0 X X
0 0 0 0 0
1 0 0 0 0
*/

/* Test case TestCase2:
clk A input sqrt busy
0 0 0 0 0
1 0 0 0 0
0 0 0 0 0
1 0 0 0 0
0 1 1 X X
1 1 1 X X
repeat (80) C 1 0 X X
0 0 0 1 0
1 0 0 1 0
*/

/* Test case TestCase3:
clk A input sqrt busy
0 0 0 0 0
1 0 0 0 0
0 0 0 0 0
1 0 0 0 0
0 4 1 X X
1 4 1 X X
repeat (80) C 4 0 X X
0 0 0 2 0
1 0 0 2 0
*/

/* Test case TestCase4:
clk A input sqrt busy
0 0 0 0 0
1 0 0 0 0
0 0 0 0 0
1 0 0 0 0
0 9 1 X X
1 9 1 X X
repeat (80) C 9 0 X X
0 0 0 3 0
1 0 0 3 0
*/

/* Test case TestCase5:
clk A input sqrt busy
0 0 0 0 0
1 0 0 0 0
0 0 0 0 0
1 0 0 0 0
0 8 1 X X
1 8 1 X X
repeat (80) C 8 0 X X
0 0 0 2 0
1 0 0 2 0
*/
