// Digital circuit 2558_1.dig as structural Verilog
module _2558_1 (
  input  clk
);

  wire add_1_c_o, and_2_out, and_3_out, and_4_out, comparator_1_eq, comparator_2_eq, comparator_3_eq,
       comparator_4_eq, comparator_5_eq, d_ff_1_nq, not_1_out, p, push_out;
  wire [1:0] multiplexer_1_out, multiplexer_3_out, multiplexer_4_out, state;
  wire [3:0] add_1_s, multiplexer_2_out, multiplexer_5_out, V;

  Button push (.out(push_out));
  D_FF d_ff_1 (.D(push_out), .C(clk), .nQ(d_ff_1_nq));  // open: Q
  and and_1 (p, push_out, d_ff_1_nq);
  Comparator #(.Bits(4)) comparator_1 (.a(V), .b(4'b1110), .eq(comparator_1_eq));  // open: gt, lt
  Comparator #(.Bits(2)) comparator_2 (.a(state), .b(2'b01), .eq(comparator_2_eq));  // open: gt, lt
  Multiplexer #(.Bits(2)) multiplexer_1 (.sel(comparator_1_eq), .in_0(state), .in_1(2'b10), .out(multiplexer_1_out));
  Add #(.Bits(4)) add_1 (.a(V), .b(4'b0011), .c_i(1'b0), .s(add_1_s), .c_o(add_1_c_o));
  and and_2 (and_2_out, comparator_2_eq, p);
  Comparator #(.Bits(2)) comparator_3 (.a(state), .b(2'b10), .eq(comparator_3_eq));  // open: gt, lt
  not not_1 (not_1_out, add_1_c_o);
  and and_3 (and_3_out, not_1_out, and_2_out);
  and and_4 (and_4_out, comparator_3_eq, p);
  Multiplexer #(.Bits(4)) multiplexer_2 (.sel(and_3_out), .in_0(V), .in_1(add_1_s), .out(multiplexer_2_out));
  Multiplexer #(.Bits(2)) multiplexer_3 (
    .sel(and_4_out), .in_0(multiplexer_1_out), .in_1(2'b00), .out(multiplexer_3_out));
  Multiplexer #(.Bits(2)) multiplexer_4 (
    .sel(comparator_4_eq), .in_0(multiplexer_3_out), .in_1(2'b01), .out(multiplexer_4_out));
  Comparator #(.Bits(2)) comparator_4 (.a(state), .b(2'b00), .eq(comparator_4_eq));  // open: gt, lt
  Multiplexer #(.Bits(4)) multiplexer_5 (
    .sel(comparator_5_eq), .in_0(multiplexer_2_out), .in_1(4'b0010), .out(multiplexer_5_out));
  Comparator #(.Bits(2)) comparator_5 (.a(state), .b(2'b00), .eq(comparator_5_eq));  // open: gt, lt
  D_FF #(.Bits(2)) d_ff_2 (.D(multiplexer_4_out), .C(clk), .Q(state));  // open: nQ
  D_FF #(.Bits(4)) d_ff_3 (.D(multiplexer_5_out), .C(clk), .Q(V));  // open: nQ
  Seven_Seg_Hex seven_seg_hex_1 (.d(V), .dp(1'b1));

  // Notes on the sheet:
  //   state
  //   00 : reset to count V =2
  //   01 : onCount
  //   10 : onDone wait for push
endmodule
