// Digital circuit 2558_2.dig as structural Verilog
module _2558_2 (
  input  [3:0] A,
  input  [3:0] B,
  input  clk,
  output [3:0] Q,
  output [3:0] R
);

  wire comparator_1_eq, multiplexer_3_out;
  wire [3:0] div_1_q, div_1_r, multiplexer_1_out, multiplexer_2_out;

  Div #(.Bits(4)) div_1 (.a(A), .b(B), .q(div_1_q), .r(div_1_r));
  Comparator #(.Bits(4)) comparator_1 (.a(B), .b(4'b0000), .eq(comparator_1_eq));  // open: gt, lt
  Multiplexer #(.Bits(4)) multiplexer_1 (.sel(comparator_1_eq), .in_0(div_1_r), .in_1(R), .out(multiplexer_1_out));
  Multiplexer #(.Bits(4)) multiplexer_2 (.sel(comparator_1_eq), .in_0(div_1_q), .in_1(Q), .out(multiplexer_2_out));
  D_FF #(.Bits(4)) d_ff_1 (.D(multiplexer_2_out), .C(clk), .Q(Q));  // open: nQ
  D_FF #(.Bits(4)) d_ff_2 (.D(multiplexer_1_out), .C(clk), .Q(R));  // open: nQ
  Seven_Seg_Hex seven_seg_hex_1 (.d(Q), .dp(multiplexer_3_out));
  Seven_Seg_Hex seven_seg_hex_2 (.d(R), .dp(multiplexer_3_out));
  Multiplexer multiplexer_3 (.sel(comparator_1_eq), .in_0(1'b1), .in_1(1'b0), .out(multiplexer_3_out));
endmodule
