// Digital circuit 2559_1.dig as structural Verilog
module _2559_1 (
  input  Clock,
  input  Wait,
  input  Car,
  input  Walk
);

  wire and_1_out, and_2_out, car_t, CG, comparator_1_eq, comparator_2_eq, comparator_3_eq, comparator_4_eq,
       comparator_5_eq, comparator_6_eq, CR, CY, d_ff_1_nq, d_ff_2_nq, d_ff_3_nq, lookuptable_1_out,
       lookuptable_2_out, lookuptable_3_out, lookuptable_4_out, lookuptable_5_out, lookuptable_6_out, s0, s1,
       s2, wait_t, walk_t, WG, WR, WY;
  wire [2:0] multiplexer_1_out, multiplexer_2_out, multiplexer_3_out, multiplexer_4_out, multiplexer_5_out,
       multiplexer_6_out, multiplexer_7_out, multiplexer_8_out, multiplexer_9_out;

  Comparator #(.Bits(3)) comparator_1 (.a({s2, s1, s0}), .b(3'b101), .eq(comparator_1_eq));  // open: gt, lt
  Multiplexer #(.Bits(3)) multiplexer_1 (
    .sel(comparator_1_eq), .in_0({s2, s1, s0}), .in_1(3'b110), .out(multiplexer_1_out));
  Comparator #(.Bits(3)) comparator_2 (.a({s2, s1, s0}), .b(3'b110), .eq(comparator_2_eq));  // open: gt, lt
  Multiplexer #(.Bits(3)) multiplexer_2 (
    .sel(comparator_2_eq), .in_0(multiplexer_1_out), .in_1(3'b001), .out(multiplexer_2_out));
  Comparator #(.Bits(3)) comparator_3 (.a({s2, s1, s0}), .b(3'b011), .eq(comparator_3_eq));  // open: gt, lt
  Multiplexer #(.Bits(3)) multiplexer_3 (
    .sel(comparator_3_eq), .in_0(multiplexer_2_out), .in_1(3'b100), .out(multiplexer_3_out));
  Comparator #(.Bits(3)) comparator_4 (.a({s2, s1, s0}), .b(3'b100), .eq(comparator_4_eq));  // open: gt, lt
  Multiplexer #(.Bits(3)) multiplexer_4 (
    .sel(comparator_4_eq), .in_0(multiplexer_3_out), .in_1(3'b010), .out(multiplexer_4_out));
  Multiplexer #(.Bits(3)) multiplexer_5 (.sel(car_t), .in_0(multiplexer_4_out), .in_1(3'b011), .out(multiplexer_5_out));
  Comparator #(.Bits(3)) comparator_5 (.a({s2, s1, s0}), .b(3'b000), .eq(comparator_5_eq));  // open: gt, lt
  Comparator #(.Bits(3)) comparator_6 (.a({s2, s1, s0}), .b(3'b000), .eq(comparator_6_eq));  // open: gt, lt
  Multiplexer #(.Bits(3)) multiplexer_6 (
    .sel(walk_t), .in_0(multiplexer_5_out), .in_1(3'b101), .out(multiplexer_6_out));
  D_FF d_ff_1 (.D(Wait), .C(Clock), .nQ(d_ff_1_nq));  // open: Q
  D_FF d_ff_2 (.D(Car), .C(Clock), .nQ(d_ff_2_nq));  // open: Q
  D_FF d_ff_3 (.D(Walk), .C(Clock), .nQ(d_ff_3_nq));  // open: Q
  and and_1 (and_1_out, car_t, comparator_5_eq);
  and and_2 (and_2_out, walk_t, comparator_6_eq);
  and and_3 (wait_t, Wait, d_ff_1_nq);
  and and_4 (car_t, Car, d_ff_2_nq);
  and and_5 (walk_t, Walk, d_ff_3_nq);
  Multiplexer #(.Bits(3)) multiplexer_7 (
    .sel(and_1_out), .in_0(multiplexer_6_out), .in_1(3'b010), .out(multiplexer_7_out));
  Multiplexer #(.Bits(3)) multiplexer_8 (
    .sel(and_2_out), .in_0(multiplexer_7_out), .in_1(3'b001), .out(multiplexer_8_out));
  Multiplexer #(.Bits(3)) multiplexer_9 (
    .sel(wait_t), .in_0(multiplexer_8_out), .in_1(3'b000), .out(multiplexer_9_out));
  D_FF #(.Bits(3)) d_ff_4 (.D(multiplexer_9_out), .C(Clock), .Q({s2, s1, s0}));  // open: nQ
  // Probe on s2
  LED led_1 (.in(CR));
  LED led_2 (.in(CY));
  LED led_3 (.in(CG));
  // Probe on {s2, s1, s0}
  // Probe on s1
  // Probe on s0
  LED led_4 (.in(WR));
  LED led_5 (.in(WY));
  LED led_6 (.in(WG));
  LookUpTable lookuptable_1 (.in0(s0), .in1(s1), .in2(s2), .out(lookuptable_1_out));
  LookUpTable lookuptable_2 (.in0(s0), .in1(s1), .in2(s2), .out(lookuptable_2_out));
  LookUpTable lookuptable_3 (.in0(s0), .in1(s1), .in2(s2), .out(lookuptable_3_out));
  LookUpTable lookuptable_4 (.in0(s0), .in1(s1), .in2(s2), .out(lookuptable_4_out));
  LookUpTable lookuptable_5 (.in0(s0), .in1(s1), .in2(s2), .out(lookuptable_5_out));
  LookUpTable lookuptable_6 (.in0(s0), .in1(s1), .in2(s2), .out(lookuptable_6_out));
  D_FF d_ff_5 (.D(lookuptable_1_out), .C(Clock), .Q(CR));  // open: nQ
  D_FF d_ff_6 (.D(lookuptable_2_out), .C(Clock), .Q(CY));  // open: nQ
  D_FF d_ff_7 (.D(lookuptable_3_out), .C(Clock), .Q(CG));  // open: nQ
  D_FF d_ff_8 (.D(lookuptable_4_out), .C(Clock), .Q(WR));  // open: nQ
  D_FF d_ff_9 (.D(lookuptable_5_out), .C(Clock), .Q(WY));  // open: nQ
  D_FF d_ff_10 (.D(lookuptable_6_out), .C(Clock), .Q(WG));  // open: nQ

  // Other names for the same wires on the sheet: clk = Clock; state[2:0] = {s2, s1, s0}

  // Notes on the sheet:
  //   Between Walk
  //   State
  //   000 : CY WY (car)
  //   001 : CR WG (idle green)
  //   010 : CG WR (idel car)
  //   car
  //   011 : CR WY
  //   100 : CR WR
  //   010 : idle car
  //   walk
  //   101 : CY WR
  //   110 : CR WR
  //   001 : idle walk
  //   Between Car
  //   Start state
  //   Force When 00
  //   Car
  //   Walk
  //   contents of lookuptable_1 (hex, n*v repeats v):
  //   0,1,0,1,1,0,1
  //   contents of lookuptable_2 (hex, n*v repeats v):
  //   1,4*0,1
  //   contents of lookuptable_3 (hex, n*v repeats v):
  //   0,0,1
  //   contents of lookuptable_4 (hex, n*v repeats v):
  //   0,0,1,0,1,1,1
  //   contents of lookuptable_5 (hex, n*v repeats v):
  //   1,0,0,1
  //   contents of lookuptable_6 (hex, n*v repeats v):
  //   0,1
endmodule
