// Digital circuit 2559_2.dig as structural Verilog
module _2559_2 (
  input  [3:0] A,
  input  clk,
  output [7:0] out_3,
  output [7:0] out_4
);

  wire [7:0] mul_1_mul;

  Mul #(.Bits(4)) mul_1 (.a(A), .b(4'b1001), .mul(mul_1_mul));
  D_FF #(.Bits(8)) d_ff_1 (.D(mul_1_mul), .C(clk), .Q(out_3));  // open: nQ
  Seven_Seg_Hex seven_seg_hex_1 (.d(out_3[7:4]), .dp(1'b1));
  Seven_Seg_Hex seven_seg_hex_2 (.d(out_3[3:0]), .dp(1'b1));

  assign out_4 = out_3;
endmodule
