// Digital circuit Template.dig as structural Verilog
module Template (
  input  A,
  input  B,
  input  Cin,
  output Sum,
  output Cout
);

  wire ab, and_1_out, and_2_out, and_3_out, and_4_out, and_5_out, and_6_out, and_7_out, bb, cb;

  not not_1 (ab, A);
  not not_2 (bb, B);
  not not_3 (cb, Cin);
  and and_1 (and_1_out, ab, bb, Cin);
  and and_2 (and_2_out, ab, B, cb);
  and and_3 (and_3_out, A, bb, cb);
  and and_4 (and_4_out, A, B, Cin);
  and and_5 (and_5_out, A, B);
  and and_6 (and_6_out, A, Cin);
  and and_7 (and_7_out, B, Cin);
  or or_1 (Sum, and_1_out, and_2_out, and_3_out, and_4_out);
  or or_2 (Cout, and_5_out, and_6_out, and_7_out);

  // Other names for the same wires on the sheet: c = Cin
endmodule
