// Digital circuit Template.dig as structural Verilog
module Template (
  input  A,
  input  B,
  input  Cin,
  output Sum,
  output Cout
);

  wire ab, and_1_out, and_2_out, bb, cb, or_1_out, or_2_out, or_3_out, or_4_out, or_5_out, or_6_out, or_7_out;

  not not_1 (ab, A);
  not not_2 (bb, B);
  not not_3 (cb, Cin);
  or or_1 (or_1_out, ab, bb, cb);
  or or_2 (or_2_out, ab, B, Cin);
  or or_3 (or_3_out, A, B, cb);
  or or_4 (or_4_out, A, bb, Cin);
  or or_5 (or_5_out, ab, cb);
  or or_6 (or_6_out, ab, bb);
  or or_7 (or_7_out, bb, cb);
  and and_1 (and_1_out, or_1_out, or_2_out, or_3_out, or_4_out);
  and and_2 (and_2_out, or_5_out, or_6_out, or_7_out);
  not not_4 (Sum, and_1_out);
  not not_5 (Cout, and_2_out);

  // Other names for the same wires on the sheet: c = Cin
endmodule
