// Digital circuit Template.dig as structural Verilog
module Template (
  input  A,
  input  B,
  input  C,
  input  D,
  output Z1,
  output Z2,
  output Z3
);

  wire ab, and_1_out, and_2_out, and_3_out, and_4_out, and_5_out, and_6_out, and_7_out, and_8_out, and_9_out,
       and_10_out, bb, cb, db;

  not not_1 (ab, A);
  not not_2 (db, D);
  not not_3 (bb, B);
  not not_4 (cb, C);
  and and_1 (and_1_out, B, cb, db);
  and and_2 (and_2_out, A, cb);
  and and_3 (and_3_out, A, B, C, db);
  and and_4 (and_4_out, ab, bb, D);
  and and_5 (and_5_out, ab, C);
  and and_6 (and_6_out, A, bb, C, D);
  and and_7 (and_7_out, A, B, C, D);
  and and_8 (and_8_out, A, bb, C, db);
  and and_9 (and_9_out, ab, B, cb, D);
  and and_10 (and_10_out, ab, bb, cb, db);
  or or_1 (Z1, and_1_out, and_2_out, and_3_out);
  or or_2 (Z2, and_4_out, and_5_out, and_6_out);
  or or_3 (Z3, and_7_out, and_8_out, and_9_out, and_10_out);
endmodule
