// Digital circuit Template.dig as structural Verilog
module Template (
  input  A,
  input  B,
  input  C,
  input  D,
  output Z2,
  output Z1,
  output Z3
);

  wire ab, bb, cb, db, or_1_out, or_2_out, or_3_out, or_4_out, or_5_out, or_6_out, or_7_out, or_8_out,
       or_9_out, or_10_out, or_11_out, or_12_out, or_13_out, or_14_out;

  not not_1 (ab, A);
  not not_2 (db, D);
  not not_3 (bb, B);
  not not_4 (cb, C);
  or or_1 (or_1_out, ab, bb);
  or or_2 (or_2_out, C, D);
  or or_3 (or_3_out, ab, B, cb, D);
  or or_4 (or_4_out, ab, B, C, db);
  or or_5 (or_5_out, A, bb, C, db);
  or or_6 (or_6_out, A, B);
  or or_7 (or_7_out, cb, db);
  or or_8 (or_8_out, ab, B, cb, D);
  or or_9 (or_9_out, A, bb, cb, D);
  or or_10 (or_10_out, A, bb, C, db);
  and and_1 (Z2, or_1_out, or_2_out, or_3_out, or_4_out, or_5_out);
  and and_2 (Z1, or_6_out, or_7_out, or_8_out, or_9_out, or_10_out);
  or or_11 (or_11_out, A, cb);
  or or_12 (or_12_out, bb, D);
  or or_13 (or_13_out, B, db);
  or or_14 (or_14_out, ab, C);
  and and_3 (Z3, or_11_out, or_12_out, or_13_out, or_14_out);
endmodule
