// Digital circuit Template.dig as structural Verilog
module Template (
  input  X0,
  input  X1,
  input  S0,
  input  X2,
  input  X3,
  input  S1,
  output Z
);

  wire A, and_1_out, and_2_out, and_3_out, and_4_out, and_5_out, and_6_out, B, not_2_out, s0b;

  not not_1 (s0b, S0);
  and and_1 (and_1_out, X0, s0b);
  and and_2 (and_2_out, X1, S0);
  and and_3 (and_3_out, X2, s0b);
  and and_4 (and_4_out, X3, S0);
  or or_1 (A, and_1_out, and_2_out);
  or or_2 (B, and_3_out, and_4_out);
  not not_2 (not_2_out, S1);
  and and_5 (and_5_out, A, not_2_out);
  and and_6 (and_6_out, B, S1);
  or or_3 (Z, and_5_out, and_6_out);
endmodule
