// Digital circuit 1_xor_with_SOP.dig as structural Verilog
module _1_xor_with_SOP (
  input  A,
  input  B,
  output out_3
);

  wire and_1_out, and_2_out, not_1_out, not_2_out;

  not not_1 (not_1_out, A);
  not not_2 (not_2_out, B);
  and and_1 (and_1_out, not_1_out, B);
  and and_2 (and_2_out, A, not_2_out);
  or or_1 (out_3, and_1_out, and_2_out);
endmodule
