// Digital circuit Template-01.dig as structural Verilog
module Template_01 (
  input  [3:0] In,
  input  in_9,
  output A,
  output E,
  output B,
  output C,
  output D,
  output F,
  output G
);

  wire and_1_out, and_2_out, and_3_out, and_4_out, and_5_out, and_6_out, and_7_out, and_8_out, and_9_out,
       and_10_out, and_11_out, and_12_out, and_13_out, and_14_out, and_15_out, and_16_out, and_17_out,
       and_18_out, and_19_out, and_20_out, and_21_out, and_22_out, and_23_out, and_24_out, and_25_out,
       and_26_out, and_27_out, and_28_out, and_29_out, wb, xb, yb, zb;

  not not_1 (wb, In[0]);
  not not_2 (zb, In[1]);
  not not_3 (yb, In[2]);
  not not_4 (xb, In[3]);
  and and_1 (and_1_out, xb, In[1], In[0]);
  and and_2 (and_2_out, yb, zb, wb);
  and and_3 (and_3_out, xb, In[1], wb);
  and and_4 (and_4_out, In[3], yb, zb);
  and and_5 (and_5_out, xb, In[2], zb, In[0]);
  and and_6 (and_6_out, xb, In[1], wb);
  and and_7 (and_7_out, yb, zb, wb);
  or or_1 (E, and_6_out, and_7_out);
  or or_2 (A, and_1_out, and_2_out, and_3_out, and_4_out, and_5_out);
  and and_8 (and_8_out, xb, zb, wb);
  and and_9 (and_9_out, xb, In[1], In[0]);
  and and_10 (and_10_out, yb, zb);
  and and_11 (and_11_out, xb, yb, In[1]);
  and and_12 (and_12_out, xb, In[2], zb, wb);
  and and_13 (and_13_out, xb, In[2], In[1]);
  and and_14 (and_14_out, yb, zb, wb);
  and and_15 (and_15_out, In[3], yb, zb);
  and and_16 (and_16_out, xb, In[2], zb, In[0]);
  or or_3 (B, and_8_out, and_9_out, and_10_out, and_11_out);
  or or_4 (F, and_12_out, and_13_out, and_14_out, and_15_out, and_16_out);
  Seven_Seg seven_seg_1 (.a(A), .b(B), .c(C), .d(D), .e(E), .f(F), .g(G), .dp(in_9));
  and and_17 (and_17_out, xb, In[1], In[0]);
  and and_18 (and_18_out, xb, In[2], wb);
  and and_19 (and_19_out, yb, zb);
  and and_20 (and_20_out, xb, In[2], zb, In[0]);
  and and_21 (and_21_out, xb, In[2], wb);
  and and_22 (and_22_out, xb, yb, In[1]);
  and and_23 (and_23_out, In[3], yb, zb);
  and and_24 (and_24_out, xb, In[2], zb, In[0]);
  or or_5 (C, and_17_out, and_18_out, and_19_out, and_20_out);
  or or_6 (G, and_21_out, and_22_out, and_23_out, and_24_out);
  and and_25 (and_25_out, yb, zb, wb);
  and and_26 (and_26_out, xb, In[1], wb);
  and and_27 (and_27_out, xb, yb, In[1]);
  and and_28 (and_28_out, In[3], yb, zb);
  and and_29 (and_29_out, xb, In[2], zb, In[0]);
  or or_7 (D, and_25_out, and_26_out, and_27_out, and_28_out, and_29_out);

  // Other names for the same wires on the sheet: w = In[0]; z = In[1]; y = In[2]; x = In[3]
endmodule
