// Digital circuit Template-02.dig as structural Verilog
module Template_02 (
  input  [2:0] In,
  input  clk,
  output [7:0] Z
);

  wire and_1_out, and_2_out, and_3_out, and_4_out, and_5_out, and_6_out, and_7_out, and_8_out, and_9_out,
       and_10_out, and_11_out, and_12_out, and_13_out, and_14_out, and_15_out, and_16_out, and_17_out,
       and_18_out, and_19_out, and_20_out, and_21_out, and_22_out, and_23_out, or_1_out, or_2_out, xb, yb, zb;

  and and_1 (and_1_out, xb, In[1], In[0]);
  and and_2 (and_2_out, xb, yb, In[0]);
  and and_3 (and_3_out, In[2], In[1], In[0]);
  and and_4 (and_4_out, yb, zb);
  and and_5 (and_5_out, In[2], yb);
  and and_6 (and_6_out, In[1], zb);
  not not_1 (Z[7], 1'b1);
  not not_2 (zb, In[0]);
  not not_3 (yb, In[1]);
  not not_4 (xb, In[2]);
  or or_1 (or_1_out, and_1_out, and_2_out, and_3_out);
  or or_2 (or_2_out, and_4_out, and_5_out, and_6_out);
  or or_3 (Z[6], or_1_out, or_2_out);
  LED led_1 (.in(Z[0]));
  LED led_2 (.in(Z[1]));
  LED led_3 (.in(Z[2]));
  LED led_4 (.in(Z[7]));
  LED led_5 (.in(Z[5]));
  LED led_6 (.in(Z[6]));
  and and_7 (and_7_out, In[2], yb, zb);
  and and_8 (and_8_out, xb, yb, In[0]);
  and and_9 (and_9_out, In[2], In[1], In[0]);
  and and_10 (and_10_out, In[1], zb);
  LED led_7 (.in(Z[3]));
  LED led_8 (.in(Z[7]));
  and and_11 (and_11_out, xb, In[1], In[0]);
  and and_12 (and_12_out, xb, yb, In[0]);
  and and_13 (and_13_out, In[2], yb);
  or or_4 (Z[5], and_7_out, and_8_out, and_9_out, and_10_out);
  Terminal terminal_1 (.D({Z[7:5], Z[7], Z[3:0]}), .C(clk), .en(1'b1));
  or or_5 (Z[3], and_11_out, and_12_out, and_13_out);
  and and_14 (and_14_out, xb, In[1], zb);
  and and_15 (and_15_out, xb, In[1], In[0]);
  and and_16 (and_16_out, yb, zb);
  and and_17 (and_17_out, In[2], yb);
  and and_18 (and_18_out, xb, In[1], zb);
  and and_19 (and_19_out, In[2], yb, zb);
  and and_20 (and_20_out, In[2], In[1], In[0]);
  or or_6 (Z[2], and_14_out, and_15_out, and_16_out, and_17_out);
  or or_7 (Z[1], and_18_out, and_19_out, and_20_out);
  and and_21 (and_21_out, In[2], yb, zb);
  and and_22 (and_22_out, xb, yb, In[0]);
  and and_23 (and_23_out, In[1], zb);
  or or_8 (Z[0], and_21_out, and_22_out, and_23_out);

  assign Z[4] = Z[7];

  // Other names for the same wires on the sheet: b = Z[6]; c = Z[5]; a = Z[7]; d = Z[7]; e = Z[3]; f = Z[2]; g = Z[1];
  //   h = Z[0]; z_t = In[0]; y = In[1]; x = In[2]
endmodule
