// Digital circuit Template-03.dig as structural Verilog
module Template_03 (
  input  [3:0] In,
  input  [1:0] Selector,
  output [3:0] Output
);

  wire and_1_out, and_2_out, and_3_out, and_4_out, and_5_out, and_6_out, and_7_out, and_8_out, and_9_out,
       and_10_out, and_11_out, and_12_out, and_13_out, and_14_out, and_15_out, and_16_out, and_17_out,
       and_18_out, and_19_out, and_20_out, and_21_out, and_22_out, and_23_out, and_24_out, and_25_out,
       and_26_out, and_27_out, and_28_out, and_29_out, and_30_out, and_31_out, i0b, i1b, i2b, i3b, or_2_out,
       or_3_out, or_5_out, or_6_out, or_8_out, or_9_out, s0b, s1b;

  not not_1 (i3b, In[0]);
  not not_2 (i2b, In[1]);
  not not_3 (i1b, In[2]);
  not not_4 (i0b, In[3]);
  not not_5 (s1b, Selector[0]);
  not not_6 (s0b, Selector[1]);
  and and_1 (and_1_out, i0b, In[1], In[0], Selector[1], Selector[0]);
  and and_2 (and_2_out, i0b, In[2], i2b, In[0], Selector[1]);
  and and_3 (and_3_out, i0b, In[2], In[1], s1b);
  and and_4 (and_4_out, i0b, In[2], In[0], s1b);
  and and_5 (and_5_out, In[3], i1b, i2b);
  and and_6 (and_6_out, i0b, In[1], i3b, Selector[1], Selector[0]);
  and and_7 (and_7_out, i0b, In[1], In[0], s0b, s1b);
  and and_8 (and_8_out, i0b, i1b, In[1], s0b, Selector[0]);
  and and_9 (and_9_out, i1b, i2b, i3b, s0b, s1b);
  and and_10 (and_10_out, i0b, i1b, In[1], Selector[1], s1b);
  and and_11 (and_11_out, i0b, In[2], i2b, In[0], s0b, Selector[0]);
  and and_12 (and_12_out, i0b, In[2], i2b, i3b, s0b);
  and and_13 (and_13_out, i0b, In[2], i2b, In[0], Selector[1]);
  and and_14 (and_14_out, In[3], i1b, i2b, Selector[1]);
  or or_1 (Output[3], and_1_out, and_2_out, and_3_out, and_4_out, and_5_out);
  or or_2 (or_2_out, and_6_out, and_7_out, and_8_out, and_9_out, and_10_out);
  or or_3 (or_3_out, and_11_out, and_12_out, and_13_out, and_14_out);
  or or_4 (Output[1], or_2_out, or_3_out);
  and and_15 (and_15_out, i0b, i3b, s0b, s1b);
  and and_16 (and_16_out, i1b, i2b, In[0], Selector[1]);
  and and_17 (and_17_out, i1b, i2b, i3b, s0b, s1b);
  and and_18 (and_18_out, i0b, In[2], i2b, In[0], s0b, Selector[0]);
  and and_19 (and_19_out, i0b, In[1], i3b, s0b);
  and and_20 (and_20_out, i1b, i2b, In[0], Selector[0]);
  and and_21 (and_21_out, i0b, In[0], Selector[1]);
  or or_5 (or_5_out, and_15_out, and_16_out, and_17_out, and_18_out);
  or or_6 (or_6_out, and_19_out, and_20_out, and_21_out);
  and and_22 (and_22_out, In[3], i1b, i2b, s0b, Selector[0]);
  and and_23 (and_23_out, In[3], i1b, i2b, Selector[1], s1b);
  and and_24 (and_24_out, i1b, i2b, In[0], s0b, s1b);
  and and_25 (and_25_out, i1b, i2b, In[0], Selector[1], Selector[0]);
  and and_26 (and_26_out, i0b, i1b, In[1], s0b, s1b);
  and and_27 (and_27_out, i0b, In[2], In[1], Selector[1]);
  and and_28 (and_28_out, i0b, In[2], i2b, In[0], s0b, Selector[0]);
  and and_29 (and_29_out, i0b, In[2], i2b, i3b, s0b);
  and and_30 (and_30_out, i0b, In[2], i3b, Selector[1]);
  and and_31 (and_31_out, i0b, In[2], In[1], Selector[0]);
  or or_7 (Output[0], or_5_out, or_6_out);
  or or_8 (or_8_out, and_22_out, and_23_out, and_24_out, and_25_out, and_26_out);
  or or_9 (or_9_out, and_27_out, and_28_out, and_29_out, and_30_out, and_31_out);
  or or_10 (Output[2], or_8_out, or_9_out);

  // Other names for the same wires on the sheet: a = Output[3]; b = Output[2]; c = Output[1]; d = Output[0];
  //   i3 = In[0]; i2 = In[1]; i1 = In[2]; i0 = In[3]; s1 = Selector[0]; s0 = Selector[1]
endmodule
