// Digital circuit Template-03_2.dig as structural Verilog
module Template_03_2 (
  input  [3:0] In,
  input  [1:0] Selector,
  output [3:0] Output
);

  wire and_1_out, and_2_out, and_3_out, and_4_out, and_5_out, and_6_out, and_7_out, and_8_out, and_9_out,
       and_10_out, and_11_out, and_12_out, and_13_out, and_14_out, and_15_out, and_16_out, and_17_out,
       and_18_out, and_19_out, and_20_out, and_21_out, and_22_out, and_23_out, and_24_out, and_25_out,
       and_26_out, and_27_out, and_28_out, and_29_out, and_30_out, and_31_out, and_32_out, and_33_out,
       and_34_out, and_35_out, and_36_out, and_37_out, and_38_out, and_39_out, and_40_out, and_41_out,
       and_42_out, and_43_out, and_44_out, and_45_out, and_46_out, and_47_out, and_48_out, and_49_out,
       and_50_out, i0b, i1b, i2b, i3b, not_7_out, not_8_out, not_10_out, not_11_out, not_12_out, not_13_out,
       not_14_out, not_15_out, not_16_out, not_17_out, not_18_out, or_1_out, or_2_out, or_3_out, or_4_out,
       or_5_out, or_6_out, or_7_out, or_8_out, s0b, s1b, w0, w1, w2, w3, x1, x2, x3, y1, y2, y3, z1, z2, z3;

  and and_1 (and_1_out, s0b, w3);
  and and_2 (and_2_out, Selector[1], x3);
  and and_3 (and_3_out, s0b, y3);
  and and_4 (and_4_out, Selector[1], z3);
  and and_5 (and_5_out, s0b, w2);
  and and_6 (and_6_out, Selector[1], x2);
  and and_7 (and_7_out, s0b, y2);
  and and_8 (and_8_out, Selector[1], z2);
  and and_9 (and_9_out, s0b, w1);
  and and_10 (and_10_out, Selector[1], x1);
  and and_11 (and_11_out, s0b, y1);
  and and_12 (and_12_out, Selector[1], z1);
  and and_13 (and_13_out, s0b, w0);
  and and_14 (and_14_out, Selector[1], In[0]);
  and and_15 (and_15_out, s0b, In[0]);
  and and_16 (and_16_out, Selector[1], In[0]);
  not not_1 (i3b, In[0]);
  not not_2 (i2b, In[1]);
  not not_3 (i1b, In[2]);
  not not_4 (i0b, In[3]);
  not not_5 (s1b, Selector[0]);
  not not_6 (s0b, Selector[1]);
  or or_1 (or_1_out, and_1_out, and_2_out);
  or or_2 (or_2_out, and_3_out, and_4_out);
  or or_3 (or_3_out, and_5_out, and_6_out);
  or or_4 (or_4_out, and_7_out, and_8_out);
  or or_5 (or_5_out, and_9_out, and_10_out);
  or or_6 (or_6_out, and_11_out, and_12_out);
  or or_7 (or_7_out, and_13_out, and_14_out);
  or or_8 (or_8_out, and_15_out, and_16_out);
  and and_17 (and_17_out, or_1_out, s1b);
  and and_18 (and_18_out, Selector[0], or_2_out);
  and and_19 (and_19_out, or_3_out, s1b);
  and and_20 (and_20_out, Selector[0], or_4_out);
  and and_21 (and_21_out, or_5_out, s1b);
  and and_22 (and_22_out, Selector[0], or_6_out);
  and and_23 (and_23_out, or_7_out, s1b);
  and and_24 (and_24_out, Selector[0], or_8_out);
  or or_9 (Output[3], and_17_out, and_18_out);
  or or_10 (Output[2], and_19_out, and_20_out);
  or or_11 (Output[1], and_21_out, and_22_out);
  or or_12 (Output[0], and_23_out, and_24_out);
  not not_7 (not_7_out, In[2]);
  not not_8 (not_8_out, In[1]);
  not not_9 (w0, In[0]);
  and and_25 (and_25_out, In[2], In[0]);
  and and_26 (and_26_out, In[2], In[1]);
  and and_27 (and_27_out, not_7_out, In[0]);
  and and_28 (and_28_out, not_7_out, In[1]);
  and and_29 (and_29_out, In[2], not_8_out, w0);
  and and_30 (and_30_out, not_8_out, w0);
  and and_31 (and_31_out, In[1], In[0]);
  LED led_1 (.in(Output[0]));
  LED led_2 (.in(Output[1]));
  LED led_3 (.in(Output[2]));
  or or_13 (w3, In[3], and_25_out, and_26_out);
  or or_14 (w2, and_27_out, and_28_out, and_29_out);
  or or_15 (w1, and_30_out, and_31_out);
  LED led_4 (.in(Output[3]));
  not not_10 (not_10_out, In[2]);
  not not_11 (not_11_out, In[1]);
  not not_12 (not_12_out, In[0]);
  and and_32 (and_32_out, In[0], In[2]);
  and and_33 (and_33_out, In[1], In[2]);
  and and_34 (and_34_out, not_12_out, In[2]);
  and and_35 (and_35_out, In[1], In[2]);
  and and_36 (and_36_out, In[0], not_11_out, In[2]);
  and and_37 (and_37_out, In[1], not_10_out);
  or or_16 (x3, and_32_out, and_33_out, In[3]);
  or or_17 (x2, and_34_out, and_35_out, In[3]);
  or or_18 (x1, and_36_out, and_37_out, In[3]);
  not not_13 (not_13_out, In[2]);
  not not_14 (not_14_out, In[1]);
  not not_15 (not_15_out, In[2]);
  not not_16 (not_16_out, In[1]);
  not not_17 (not_17_out, In[0]);
  and and_38 (and_38_out, In[2], In[0]);
  and and_39 (and_39_out, In[2], In[1]);
  and and_40 (and_40_out, In[2], not_17_out);
  and and_41 (and_41_out, In[2], In[1]);
  and and_42 (and_42_out, not_13_out, In[1]);
  and and_43 (and_43_out, In[2], not_14_out, In[0]);
  not not_18 (not_18_out, In[0]);
  and and_44 (and_44_out, In[2], In[0]);
  and and_45 (and_45_out, In[1], In[0]);
  and and_46 (and_46_out, not_15_out, not_16_out, In[0]);
  and and_47 (and_47_out, In[2], not_18_out);
  and and_48 (and_48_out, In[2], In[1]);
  and and_49 (and_49_out, In[2], not_16_out, In[0]);
  and and_50 (and_50_out, In[1], not_18_out);
  or or_19 (y3, In[3], and_38_out, and_39_out);
  or or_20 (y2, In[3], and_40_out, and_41_out);
  or or_21 (y1, In[3], and_42_out, and_43_out);
  or or_22 (z3, In[3], and_44_out, and_45_out);
  or or_23 (z2, and_46_out, and_47_out, and_48_out);
  or or_24 (z1, In[3], and_49_out, and_50_out);

  // Other names for the same wires on the sheet: i3 = In[0]; x0 = In[0]; y0 = In[0]; z0 = In[0]; i2 = In[1];
  //   i1 = In[2]; i0 = In[3]; s1 = Selector[0]; s0 = Selector[1]
endmodule
