// Digital circuit Template-04.dig as structural Verilog
module Template_04 (
  input  [6:0] In,
  output [6:0] Output
);

  wire b1, b2, b3, b4, b5, b6, b7, c1, c1b, c2, c2b, c3, c3b;

  xor xor_1 (c1, In[3], In[2], In[1], In[0]);
  xor xor_2 (c2, In[5], In[4], In[1], In[0]);
  xor xor_3 (c3, In[6], In[4], In[2], In[0]);
  not not_1 (c1b, c1);
  not not_2 (c2b, c2);
  not not_3 (c3b, c3);
  and and_1 (b1, c1b, c2b, c3);
  and and_2 (b2, c1b, c2, c3b);
  and and_3 (b3, c1b, c2, c3);
  and and_4 (b4, c1, c2b, c3b);
  and and_5 (b5, c1, c2b, c3);
  and and_6 (b6, c1, c2, c3b);
  and and_7 (b7, c1, c2, c3);
  xor xor_4 (Output[6], b1, In[6]);
  xor xor_5 (Output[5], b2, In[5]);
  xor xor_6 (Output[4], b3, In[4]);
  xor xor_7 (Output[3], b4, In[3]);
  xor xor_8 (Output[2], b5, In[2]);
  xor xor_9 (Output[1], b6, In[1]);
  xor xor_10 (Output[0], b7, In[0]);

  // Other names for the same wires on the sheet: _7 = In[0]; _6 = In[1]; _5 = In[2]; _4 = In[3]; _3 = In[4];
  //   _2 = In[5]; _1 = In[6]; o1 = Output[6]; o2 = Output[5]; o3 = Output[4]; o4 = Output[3]; o5 = Output[2];
  //   o6 = Output[1]; o7 = Output[0]
endmodule
