// Digital circuit fullAdder_2_Board.dig as structural Verilog
module fullAdder_2_Board (
  input  A,
  input  B,
  input  Cin,
  output Sum,
  output Cout
);

  wire _7400_1_pin6, _7400_2_pin3, _7400_2_pin6, _7400_2_pin10, o1, o2, o3;

  _7400 _7400_1 (
    .pin1(A), .pin2(B), .pin3(o1), .pin4(o2), .pin5(o3), .pin6(_7400_1_pin6), .pin7(1'b0), .pin8(o3),
    .pin9(o1), .pin10(B), .pin11(o2), .pin12(o1), .pin13(A), .pin14(1'b1));
  _7400 _7400_2 (
    .pin1(_7400_1_pin6), .pin2(Cin), .pin3(_7400_2_pin3), .pin4(_7400_2_pin3), .pin5(_7400_1_pin6),
    .pin6(_7400_2_pin6), .pin7(1'b0), .pin8(Sum), .pin9(_7400_2_pin6), .pin10(_7400_2_pin10),
    .pin11(_7400_2_pin10), .pin12(Cin), .pin13(_7400_2_pin3), .pin14(1'b1));
  _7400 _7400_3 (
    .pin1(_7400_2_pin3), .pin2(o1), .pin3(Cout), .pin4(1'b0), .pin5(1'b0), .pin7(1'b0), .pin9(1'b0),
    .pin10(1'b0), .pin12(1'b0), .pin13(1'b0), .pin14(1'b1));  // open: pin6, pin8, pin11

  // Other names for the same wires on the sheet: c = Cin
endmodule
