// Digital circuit diglab_05_02_temp.dig as structural Verilog
module diglab_05_02_temp (
  input  A,
  input  B,
  input  C,
  input  D,
  input  E,
  output Before,
  output After
);

  wire Ab, and_1_out, and_2_out, and_3_out, and_4_out, and_5_out, and_6_out, and_7_out, and_8_out, Bb, Cb,
       Db, Eb;

  not not_1 (Ab, A);
  not not_2 (Bb, B);
  not not_3 (Cb, C);
  not not_4 (Db, D);
  not not_5 (Eb, E);
  and and_1 (and_1_out, C, Db, Eb);
  and and_2 (and_2_out, Bb, Cb, Db);
  and and_3 (and_3_out, Ab, D, E);
  and and_4 (and_4_out, C, Db, Eb);
  and and_5 (and_5_out, Bb, Cb, Db);
  and and_6 (and_6_out, Ab, D, E);
  and and_7 (and_7_out, Bb, Db, Eb);
  and and_8 (and_8_out, Ab, Bb, Cb, E);
  or or_1 (Before, and_1_out, and_2_out, and_3_out);
  or or_2 (After, and_4_out, and_5_out, and_6_out, and_7_out, and_8_out);
endmodule

/* Test case 00000 00100:
A B C D E Before After
0 0 0 0 0 1 1
0 0 1 0 0 1 1
0 0 0 0 1 1 1
0 0 0 1 1 1 1
1 0 0 0 0 1 1
1 0 1 0 0 1 1
*/

/* Test case 00001 00011:
A B C D E Before After
0 0 0 0 1 1 1
0 0 0 1 1 1 1
0 0 0 0 1 1 1
0 0 0 1 1 1 1
0 0 0 0 1 1 1
0 0 0 1 1 1 1
0 0 0 0 1 1 1
0 0 0 1 1 1 1
*/

/* Test case 10000 10100:
A B C D E Before After
1 0 0 0 0 1 1
1 0 1 0 0 1 1
1 0 0 0 0 1 1
1 0 1 0 0 1 1
1 0 0 0 0 1 1
1 0 1 0 0 1 1
1 0 0 0 0 1 1
1 0 1 0 0 1 1
*/
