// Digital circuit 8-01.dig as structural Verilog
module _8_01 (
  input  P,
  input  T,
  input  D,
  input  C,
  input  B,
  input  A,
  input  Clr,
  input  Load,
  input  Clock,
  output QD,
  output QC,
  output QB,
  output QA,
  output RCO
);

  wire and_1_out, not_1_out, not_2_out;
  wire [3:0] add_s, multiplexer_1_out, multiplexer_2_out, multiplexer_3_out;

  Multiplexer #(.Bits(4)) multiplexer_1 (
    .sel(not_1_out), .in_0(multiplexer_2_out), .in_1(4'b0000), .out(multiplexer_1_out));
  Add #(.Bits(4)) add (.a({QD, QC, QB, QA}), .b(4'b0001), .c_i(1'b0), .s(add_s), .c_o(RCO));
  not not_1 (not_1_out, Clr);
  and and_1 (and_1_out, P, T);
  Multiplexer #(.Bits(4)) multiplexer_2 (
    .sel(and_1_out), .in_0({QD, QC, QB, QA}), .in_1(add_s), .out(multiplexer_2_out));
  Multiplexer #(.Bits(4)) multiplexer_3 (
    .sel(not_2_out), .in_0(multiplexer_1_out), .in_1({D, C, B, A}), .out(multiplexer_3_out));
  not not_2 (not_2_out, Load);
  D_FF #(.Bits(4)) d_ff_1 (.D(multiplexer_3_out), .C(Clock), .Q({QD, QC, QB, QA}));  // open: nQ
endmodule
