// Digital circuit 8-02 - Copy.dig as structural Verilog
module _8_02___Copy (
  input  A,
  input  B,
  input  Clock,
  input  Clr,
  output Z
);

  wire add_1_c_o, add_1_s, clr_t, multiplexer_2_out, r;

  not not_1 (clr_t, Clr);
  Add add_1 (.a(A), .b(B), .c_i(r), .s(add_1_s), .c_o(add_1_c_o));
  Multiplexer multiplexer_1 (.sel(clr_t), .in_0(add_1_s), .in_1(1'b0), .out(Z));
  Multiplexer multiplexer_2 (.sel(clr_t), .in_0(add_1_c_o), .in_1(1'b0), .out(multiplexer_2_out));
  D_FF d_ff_1 (.D(multiplexer_2_out), .C(Clock), .Q(r));  // open: nQ

  // Other names for the same wires on the sheet: clk = Clock
endmodule
