// Digital circuit 8-02.dig as structural Verilog
module _8_02 (
  input  A,
  input  B,
  input  Clr,
  input  Clock,
  output Z
);

  wire add_1_c_o, add_1_s, c, d_ff_1_q;

  D_FF d_ff_1 (.D(c), .C(Clock), .Q(d_ff_1_q));  // open: nQ
  Add add_1 (.a(A), .b(B), .c_i(d_ff_1_q), .s(add_1_s), .c_o(add_1_c_o));
  Multiplexer multiplexer_1 (.sel(Clr), .in_0(1'b0), .in_1(add_1_c_o), .out(c));
  Multiplexer multiplexer_2 (.sel(Clr), .in_0(1'b0), .in_1(add_1_s), .out(Z));
endmodule
