// Digital circuit 8-03 - Copy.dig as structural Verilog
module _8_03___Copy (
  input  P,
  input  clock,
  input  Clr,
  output Z
);

  wire and_1_out, d_ff_1_nq, multiplexer_1_out;

  D_FF d_ff_1 (.D(P), .C(clock), .nQ(d_ff_1_nq));  // open: Q
  and and_1 (and_1_out, P, d_ff_1_nq);
  Multiplexer multiplexer_1 (.sel(Clr), .in_0(and_1_out), .in_1(1'b0), .out(multiplexer_1_out));
  D_FF d_ff_2 (.D(multiplexer_1_out), .C(clock), .Q(Z));  // open: nQ
endmodule
