// Digital circuit 8-04.dig as structural Verilog
module _8_04 (
  input  P,
  input  clock,
  input  Clr,
  output Z
);

  wire and_1_out, and_2_out, not_1_out, old_P_nq, Z_q;

  not not_1 (not_1_out, Clr);
  and and_1 (and_1_out, P, not_1_out);
  D_FF old_P (.D(and_1_out), .C(clock), .nQ(old_P_nq));  // open: Q
  and and_2 (and_2_out, and_1_out, old_P_nq);
  D_FF u_Z (.D(and_2_out), .C(clock), .Q(Z_q));  // open: nQ
  D_FF d_ff_1 (.D(Z_q), .C(clock), .Q(Z));  // open: nQ
endmodule
