// Digital circuit 8-05 - Copy.dig as structural Verilog
module _8_05___Copy (
  input  P,
  input  clock,
  input  Clr,
  output Z
);

  wire and_1_out, not_1_out, old_P_nq, P_q;

  not not_1 (not_1_out, Clr);
  and and_1 (and_1_out, P, not_1_out);
  D_FF u_P (.D(and_1_out), .C(clock), .Q(P_q));  // open: nQ
  D_FF old_P (.D(P_q), .C(clock), .nQ(old_P_nq));  // open: Q
  and and_2 (Z, P_q, old_P_nq);
endmodule
