// Digital circuit ans.dig as structural Verilog
module ans (
  input  P5,
  input  Pcoffee,
  input  Ptea,
  input  Pnext,
  input  Pchange,
  input  reset,
  input  clock,
  input  P10,
  input  P20,
  output [5:0] Balance,
  output CoffeeOut,
  output TeaOut,
  output [1:0] Change5,
  output [1:0] Change10,
  output [1:0] Change20
);

  wire add_1_c_o, add_2_c_o, add_3_c_o, add_4_c_o, add_5_c_o, add_6_c_o, add_7_c_o, add_8_c_o, add_9_c_o,
       add_10_c_o, add_11_c_o, add_12_c_o, comparator_1_eq, comparator_1_gt, comparator_1_lt, d_ff_1_q,
       d_ff_2_q, d_ff_3_q, d_ff_4_nq, d_ff_5_nq, d_ff_6_nq, d_ff_7_q, d_ff_8_nq, resett;
  wire [2:0] ppp;
  wire [5:0] add_1_s, add_2_s, add_3_s, add_4_s, add_5_s, add_6_s, add_7_s, add_8_s, add_9_s, add_10_s,
       add_11_s, add_12_s, ans5, ans10, ans15, ans20, ans25, ans30, ans35, multiplexer_4_out,
       multiplexer_5_out, multiplexer_6_out, multiplexer_7_out, multiplexer_14_out, multiplexer_16_out,
       multiplexer_17_out, multiplexer_18_out, p5_t, p10_t, p20_t;

  D_FF d_ff_1 (.D(P5), .C(clock), .Q(d_ff_1_q));  // open: nQ
  D_FF d_ff_2 (.D(P10), .C(clock), .Q(d_ff_2_q));  // open: nQ
  D_FF d_ff_3 (.D(P20), .C(clock), .Q(d_ff_3_q));  // open: nQ
  D_FF d_ff_4 (.D(d_ff_1_q), .C(clock), .nQ(d_ff_4_nq));  // open: Q
  D_FF d_ff_5 (.D(d_ff_2_q), .C(clock), .nQ(d_ff_5_nq));  // open: Q
  D_FF d_ff_6 (.D(d_ff_3_q), .C(clock), .nQ(d_ff_6_nq));  // open: Q
  and and_1 (ppp[0], d_ff_1_q, d_ff_4_nq);
  D_FF d_ff_7 (.D(reset), .C(clock), .Q(d_ff_7_q));  // open: nQ
  and and_2 (ppp[1], d_ff_2_q, d_ff_5_nq);
  and and_3 (ppp[2], d_ff_3_q, d_ff_6_nq);
  Multiplexer #(.Bits(6)) multiplexer_1 (.sel(ppp[0]), .in_0({6{1'b0}}), .in_1(6'b000101), .out(p5_t));
  Multiplexer #(.Bits(6)) multiplexer_2 (.sel(ppp[1]), .in_0({6{1'b0}}), .in_1(6'b001010), .out(p10_t));
  Multiplexer #(.Bits(6)) multiplexer_3 (.sel(ppp[2]), .in_0({6{1'b0}}), .in_1(6'b010100), .out(p20_t));
  D_FF d_ff_8 (.D(d_ff_7_q), .C(clock), .nQ(d_ff_8_nq));  // open: Q
  // Probe on Pcoffee
  // Probe on Ptea
  // Probe on Pnext
  // Probe on Pchange
  and and_4 (resett, d_ff_7_q, d_ff_8_nq);
  // Probe on resett
  Add #(.Bits(6)) add_1 (.a(Balance), .b(p5_t), .c_i(1'b0), .s(add_1_s), .c_o(add_1_c_o));
  Add #(.Bits(6)) add_2 (.a(Balance), .b(p5_t), .c_i(1'b0), .s(add_2_s), .c_o(add_2_c_o));
  Add #(.Bits(6)) add_3 (.a(Balance), .b(p10_t), .c_i(1'b0), .s(add_3_s), .c_o(add_3_c_o));
  Add #(.Bits(6)) add_4 (.a(Balance), .b(p5_t), .c_i(1'b0), .s(add_4_s), .c_o(add_4_c_o));
  Add #(.Bits(6)) add_5 (.a(Balance), .b(p5_t), .c_i(1'b0), .s(add_5_s), .c_o(add_5_c_o));
  Add #(.Bits(6)) add_6 (.a(Balance), .b(p10_t), .c_i(1'b0), .s(add_6_s), .c_o(add_6_c_o));
  Add #(.Bits(6)) add_7 (.a(Balance), .b(p20_t), .c_i(1'b0), .s(add_7_s), .c_o(add_7_c_o));
  Multiplexer #(.Bits(6)) multiplexer_4 (.sel(add_1_c_o), .in_0(add_1_s), .in_1(Balance), .out(multiplexer_4_out));
  Multiplexer #(.Bits(6)) multiplexer_5 (.sel(add_2_c_o), .in_0(add_2_s), .in_1(Balance), .out(multiplexer_5_out));
  Multiplexer #(.Bits(6)) multiplexer_6 (.sel(add_3_c_o), .in_0(add_3_s), .in_1(Balance), .out(multiplexer_6_out));
  Multiplexer #(.Bits(6)) multiplexer_7 (.sel(add_4_c_o), .in_0(add_4_s), .in_1(Balance), .out(multiplexer_7_out));
  Multiplexer #(.Bits(6)) multiplexer_8 (.sel(add_5_c_o), .in_0(add_5_s), .in_1(Balance), .out(ans5));
  Multiplexer #(.Bits(6)) multiplexer_9 (.sel(add_6_c_o), .in_0(add_6_s), .in_1(Balance), .out(ans10));
  Multiplexer #(.Bits(6)) multiplexer_10 (.sel(add_7_c_o), .in_0(add_7_s), .in_1({6{1'b0}}), .out(ans20));
  Add #(.Bits(6)) add_8 (.a(multiplexer_4_out), .b(p10_t), .c_i(1'b0), .s(add_8_s), .c_o(add_8_c_o));
  Add #(.Bits(6)) add_9 (.a(multiplexer_5_out), .b(p20_t), .c_i(1'b0), .s(add_9_s), .c_o(add_9_c_o));
  Add #(.Bits(6)) add_10 (.a(multiplexer_6_out), .b(p20_t), .c_i(1'b0), .s(add_10_s), .c_o(add_10_c_o));
  Add #(.Bits(6)) add_11 (.a(multiplexer_7_out), .b(p10_t), .c_i(1'b0), .s(add_11_s), .c_o(add_11_c_o));
  Multiplexer #(.Bits(6)) multiplexer_11 (.sel(add_8_c_o), .in_0(add_8_s), .in_1(multiplexer_4_out), .out(ans15));
  Multiplexer #(.Bits(6)) multiplexer_12 (.sel(add_9_c_o), .in_0(add_9_s), .in_1(multiplexer_5_out), .out(ans25));
  Multiplexer #(.Bits(6)) multiplexer_13 (.sel(add_10_c_o), .in_0(add_10_s), .in_1(multiplexer_6_out), .out(ans30));
  Multiplexer #(.Bits(6)) multiplexer_14 (
    .sel(add_11_c_o), .in_0(add_11_s), .in_1(multiplexer_7_out), .out(multiplexer_14_out));
  Add #(.Bits(6)) add_12 (.a(multiplexer_14_out), .b(p20_t), .c_i(1'b0), .s(add_12_s), .c_o(add_12_c_o));
  Multiplexer #(.Bits(6)) multiplexer_15 (.sel(add_12_c_o), .in_0(add_12_s), .in_1(multiplexer_14_out), .out(ans35));
  Multiplexer #(.Bits(6), .Selector_Bits(3)) multiplexer_16 (
    .sel(ppp), .in_0(Balance), .in_1(ans5), .in_2(ans10), .in_3(ans15), .in_4(ans20), .in_5(ans25),
    .in_6(ans30), .in_7(ans35), .out(multiplexer_16_out));
  Comparator #(.Bits(6)) comparator_1 (
    .a(multiplexer_16_out), .b(6'b110010), .gt(comparator_1_gt), .eq(comparator_1_eq), .lt(comparator_1_lt));
  // Probe on comparator_1_eq
  // Probe on comparator_1_lt
  Multiplexer #(.Bits(6)) multiplexer_17 (
    .sel(comparator_1_gt), .in_0(multiplexer_16_out), .in_1(6'b110010), .out(multiplexer_17_out));
  Multiplexer #(.Bits(6)) multiplexer_18 (
    .sel(resett), .in_0(multiplexer_17_out), .in_1({6{1'b0}}), .out(multiplexer_18_out));
  D_FF #(.Bits(6)) d_ff_9 (.D(multiplexer_18_out), .C(clock), .Q(Balance));  // open: nQ
  // Probe on Balance

  assign Change5 = 2'b00;
  assign Change10 = 2'b00;
  assign Change20 = 2'b00;
  assign CoffeeOut = 1'b0;
  assign TeaOut = 1'b0;

  // Other names for the same wires on the sheet: clk = clock; oldB[5:0] = Balance
endmodule
