// Digital circuit lab9.dig as structural Verilog
module lab9 (
  input  P5,
  input  Pcoffee,
  input  Ptea,
  input  Pnext,
  input  Pchange,
  input  reset,
  input  clock,
  input  P10,
  input  P20,
  output [5:0] Balance,
  output CoffeeOut,
  output TeaOut,
  output [1:0] Change5,
  output [1:0] Change10,
  output [1:0] Change20
);

  wire add_3_c_o;
  wire [1:0] add_1_c_o;
  wire [5:0] add_1_s, add_2_s, add_3_s, multiplexer_4_out, multiplexer_5_out, multiplexer_6_out,
       multiplexer_7_out, multiplexer_8_out, multiplexer_9_out, p5_t, p10_t, p20_t;

  Multiplexer #(.Bits(6)) multiplexer_1 (.sel(P5), .in_0({6{1'b0}}), .in_1(6'b000101), .out(p5_t));
  Multiplexer #(.Bits(6)) multiplexer_2 (.sel(P10), .in_0({6{1'b0}}), .in_1(6'b001010), .out(p10_t));
  Multiplexer #(.Bits(6)) multiplexer_3 (.sel(P20), .in_0({6{1'b0}}), .in_1(6'b010100), .out(p20_t));
  Add #(.Bits(6)) add_1 (.a(Balance), .b(p5_t), .c_i(1'b0), .s(add_1_s), .c_o(add_1_c_o[0]));
  Multiplexer #(.Bits(6)) multiplexer_4 (.sel(add_1_c_o[0]), .in_0(add_1_s), .in_1({6{1'b0}}), .out(multiplexer_4_out));
  Multiplexer #(.Bits(6)) multiplexer_5 (.sel(add_1_c_o[0]), .in_0(p10_t), .in_1({6{1'b0}}), .out(multiplexer_5_out));
  Add #(.Bits(6)) add_2 (.a(Balance), .b(multiplexer_5_out), .c_i(1'b0), .s(add_2_s), .c_o(add_1_c_o[1]));
  // Probe on Pcoffee
  // Probe on Ptea
  // Probe on Pnext
  // Probe on Pchange
  // Probe on reset
  Multiplexer #(.Bits(6)) multiplexer_6 (.sel(add_1_c_o[1]), .in_0(add_2_s), .in_1({6{1'b0}}), .out(multiplexer_6_out));
  Multiplexer #(.Bits(6)) multiplexer_7 (.sel(add_1_c_o[1]), .in_0(p20_t), .in_1({6{1'b0}}), .out(multiplexer_7_out));
  Add #(.Bits(6)) add_3 (.a(Balance), .b(multiplexer_7_out), .c_i(1'b0), .s(add_3_s), .c_o(add_3_c_o));
  Multiplexer #(.Bits(6)) multiplexer_8 (.sel(add_3_c_o), .in_0(add_3_s), .in_1({6{1'b0}}), .out(multiplexer_8_out));
  Multiplexer #(.Bits(6), .Selector_Bits(2)) multiplexer_9 (
    .sel(add_1_c_o), .in_0(multiplexer_4_out), .in_1(multiplexer_6_out), .in_2(multiplexer_8_out),
    .in_3(Balance), .out(multiplexer_9_out));
  D_FF #(.Bits(6)) d_ff_1 (.D(multiplexer_9_out), .C(clock), .Q(Balance));  // open: nQ
  // Probe on Balance

  assign Change5 = 2'b00;
  assign Change10 = 2'b00;
  assign Change20 = 2'b00;
  assign CoffeeOut = 1'b0;
  assign TeaOut = 1'b0;

  // Other names for the same wires on the sheet: clk = clock; oldB[5:0] = Balance
endmodule
