// Digital circuit lab9_sepinput.dig as structural Verilog
module lab9_sepinput (
  input  P5,
  input  Pcoffee,
  input  Ptea,
  input  Pnext,
  input  Pchange,
  input  reset,
  input  clock,
  input  P10,
  input  P20,
  output [5:0] Balance,
  output CoffeeOut,
  output TeaOut,
  output [1:0] Change5,
  output [1:0] Change10,
  output [1:0] Change20
);

  wire add_1_c_o, add_2_c_o, add_3_c_o, comparator_1_eq, comparator_1_gt, comparator_1_lt, d_ff_1_q,
       d_ff_2_q, d_ff_3_q, d_ff_4_nq, d_ff_5_nq, d_ff_6_nq;
  wire [2:0] ppp;
  wire [5:0] add_1_s, add_2_s, add_3_s, multiplexer_4_out, multiplexer_5_out, multiplexer_6_out,
       multiplexer_7_out, multiplexer_8_out, p5_t, p10_t, p20_t;

  D_FF d_ff_1 (.D(P5), .C(clock), .Q(d_ff_1_q));  // open: nQ
  D_FF d_ff_2 (.D(P10), .C(clock), .Q(d_ff_2_q));  // open: nQ
  D_FF d_ff_3 (.D(P20), .C(clock), .Q(d_ff_3_q));  // open: nQ
  D_FF d_ff_4 (.D(d_ff_1_q), .C(clock), .nQ(d_ff_4_nq));  // open: Q
  D_FF d_ff_5 (.D(d_ff_2_q), .C(clock), .nQ(d_ff_5_nq));  // open: Q
  D_FF d_ff_6 (.D(d_ff_3_q), .C(clock), .nQ(d_ff_6_nq));  // open: Q
  and and_1 (ppp[0], d_ff_1_q, d_ff_4_nq);
  and and_2 (ppp[1], d_ff_2_q, d_ff_5_nq);
  and and_3 (ppp[2], d_ff_3_q, d_ff_6_nq);
  Multiplexer #(.Bits(6)) multiplexer_1 (.sel(ppp[0]), .in_0({6{1'b0}}), .in_1(6'b000101), .out(p5_t));
  Multiplexer #(.Bits(6)) multiplexer_2 (.sel(ppp[1]), .in_0({6{1'b0}}), .in_1(6'b001010), .out(p10_t));
  Multiplexer #(.Bits(6)) multiplexer_3 (.sel(ppp[2]), .in_0({6{1'b0}}), .in_1(6'b010100), .out(p20_t));
  // Probe on Pcoffee
  // Probe on Ptea
  // Probe on Pnext
  // Probe on Pchange
  // Probe on reset
  Add #(.Bits(6)) add_1 (.a(Balance), .b(p5_t), .c_i(1'b0), .s(add_1_s), .c_o(add_1_c_o));
  Add #(.Bits(6)) add_2 (.a(Balance), .b(p10_t), .c_i(1'b0), .s(add_2_s), .c_o(add_2_c_o));
  Add #(.Bits(6)) add_3 (.a(Balance), .b(p20_t), .c_i(1'b0), .s(add_3_s), .c_o(add_3_c_o));
  Multiplexer #(.Bits(6)) multiplexer_4 (.sel(add_1_c_o), .in_0(add_1_s), .in_1({6{1'b0}}), .out(multiplexer_4_out));
  Multiplexer #(.Bits(6)) multiplexer_5 (.sel(add_2_c_o), .in_0(add_2_s), .in_1({6{1'b0}}), .out(multiplexer_5_out));
  Multiplexer #(.Bits(6)) multiplexer_6 (.sel(add_3_c_o), .in_0(add_3_s), .in_1({6{1'b0}}), .out(multiplexer_6_out));
  Multiplexer #(.Bits(6), .Selector_Bits(3)) multiplexer_7 (
    .sel(ppp), .in_0(Balance), .in_1(multiplexer_4_out), .in_2(multiplexer_5_out), .in_3(multiplexer_4_out),
    .in_4(multiplexer_6_out), .in_5(multiplexer_4_out), .in_6(multiplexer_5_out), .in_7(multiplexer_4_out),
    .out(multiplexer_7_out));
  Comparator #(.Bits(6)) comparator_1 (
    .a(multiplexer_7_out), .b(6'b110010), .gt(comparator_1_gt), .eq(comparator_1_eq), .lt(comparator_1_lt));
  Multiplexer #(.Bits(6)) multiplexer_8 (
    .sel(comparator_1_gt), .in_0(multiplexer_7_out), .in_1(6'b110010), .out(multiplexer_8_out));
  // Probe on comparator_1_eq
  // Probe on comparator_1_lt
  D_FF #(.Bits(6)) d_ff_7 (.D(multiplexer_8_out), .C(clock), .Q(Balance));  // open: nQ
  // Probe on Balance

  assign Change5 = 2'b00;
  assign Change10 = 2'b00;
  assign Change20 = 2'b00;
  assign CoffeeOut = 1'b0;
  assign TeaOut = 1'b0;

  // Other names for the same wires on the sheet: clk = clock; oldB[5:0] = Balance
endmodule
