// Digital circuit 1-2.dig as structural Verilog
module _1_2 (
  input  X0,
  input  X1,
  input  X2,
  input  X3,
  input  S0,
  input  S1,
  output Z
);

  wire _00, _11, aa, and_1_out, and_2_out, and_3_out, and_4_out, and_5_out, and_6_out, bb, cc, dd, X, Y;

  not not_1 (aa, X0);
  not not_2 (bb, X1);
  not not_3 (cc, X2);
  not not_4 (dd, X3);
  not not_5 (_00, S0);
  not not_6 (_11, S1);
  and and_1 (and_1_out, _00, X0);
  and and_2 (and_2_out, S0, X1);
  and and_3 (and_3_out, _00, X2);
  and and_4 (and_4_out, S0, X3);
  and and_5 (and_5_out, _11, X);
  and and_6 (and_6_out, S1, Y);
  or or_1 (X, and_1_out, and_2_out);
  or or_2 (Y, and_3_out, and_4_out);
  or or_3 (Z, and_5_out, and_6_out);

  // Other names for the same wires on the sheet: _0 = S0; _1 = S1; a = X0; b = X1; c = X2; d = X3
endmodule
