// Digital circuit mid0.dig as structural Verilog
module mid0 (
  input  [2:0] A,
  input  [2:0] B,
  output Z
);

  wire and_1_out, and_2_out, and_3_out, or_1_out;

  and and_1 (and_1_out, A[1], A[0], B[0]);
  and and_2 (and_2_out, A[1], B[1]);
  and and_3 (and_3_out, A[0], B[1], B[0]);
  or or_1 (or_1_out, A[2], and_1_out, and_2_out, and_3_out, B[2]);
  not not_1 (Z, or_1_out);
  Seven_Seg seven_seg_1 (.a(Z), .b(1'b1), .c(1'b1), .d(Z), .e(Z), .f(Z), .g(1'b0), .dp(1'b0));

  // Other names for the same wires on the sheet: c = A[0]; b_t = A[1]; a_t = A[2]; f = B[0]; e = B[1]; d = B[2]
endmodule

/* Test case:
A B Z
0 0 1
0 1 1
1 0 1
2 0 1
0 2 1
3 0 1
0 3 1
2 1 1
1 2 1
*/
