// Digital circuit mid1.dig as structural Verilog
module mid1 (
  input  [2:0] S,
  output O1,
  output O2
);

  wire decoder_1_out_0, decoder_1_out_1, decoder_1_out_2, decoder_1_out_3, decoder_1_out_4, decoder_1_out_5,
       decoder_1_out_6, decoder_1_out_7;

  Decoder #(.Selector_Bits(3)) decoder_1 (
    .out_0(decoder_1_out_0), .out_1(decoder_1_out_1), .out_2(decoder_1_out_2), .out_3(decoder_1_out_3),
    .out_4(decoder_1_out_4), .out_5(decoder_1_out_5), .out_6(decoder_1_out_6), .out_7(decoder_1_out_7));  // open: sel
  // Probe on decoder_1_out_1
  // Probe on decoder_1_out_3
  // Probe on O1
  or or_1 (O1, decoder_1_out_6, decoder_1_out_5, decoder_1_out_4, decoder_1_out_2);
  or or_2 (O2, decoder_1_out_7, decoder_1_out_6, decoder_1_out_4, decoder_1_out_2, decoder_1_out_0);
  // Probe on O2
endmodule

/* Test case:
S O1 O2
0 0 1
1 0 0
2 1 1
3 0 0
4 1 1
5 1 0
6 1 1
7 0 1
*/
