// Digital circuit mid3.dig as structural Verilog
module mid3 (
  input  [2:0] in1,
  input  as,
  input  [2:0] in2,
  output [2:0] O
);

  wire add_1_c_o, add_2_c_o;
  wire [2:0] i, ii, not_1_out, o1, o2;

  Multiplexer #(.Bits(3), .Selector_Bits(3)) multiplexer_1 (
    .sel(in1), .in_0(3'b000), .in_1(3'b001), .in_2(3'b001), .in_3(3'b010), .in_4(3'b001), .in_5(3'b010),
    .in_6(3'b010), .in_7(3'b011), .out(i));
  Multiplexer #(.Selector_Bits(3), .Bits(3)) multiplexer_2 (
    .sel(in2), .in_0(3'b000), .in_1(3'b001), .in_2(3'b001), .in_3(3'b010), .in_4(3'b001), .in_5(3'b010),
    .in_6(3'b010), .in_7(3'b011), .out(ii));
  Neg neg_1 ();  // open: in, out
  Add #(.Bits(3)) add_1 (.a(i), .b(ii), .c_i(1'b0), .s(o1), .c_o(add_1_c_o));
  Multiplexer #(.Bits(3)) multiplexer_3 (.sel(as), .in_0(o1), .in_1(o2), .out(O));
  // Probe on add_1_c_o
  assign not_1_out = ~ii;  // Not not_1, 3 bits wide
  Add #(.Bits(3)) add_2 (.a(i), .b(not_1_out), .c_i(1'b1), .s(o2), .c_o(add_2_c_o));
  // Probe on add_2_c_o
endmodule

/* Test case:
in1 in2 as O
011 010 1 001
111 001 0 100
*/

/* Test case:
in1 in2 as O
110 001 0 011
*/
